// Logisim project ALUwithVincen.circ as structural Verilog
module half_adder (
  input  A,
  input  B,
  output S,
  output Cout
);

  and and_1 (Cout, A, B);
  xor xor_1 (S, A, B);
endmodule

module full_adder (
  input  A,
  input  B,
  input  Cin,
  output S,
  output Cout
);

  wire half_adder_1_cout, half_adder_1_s, half_adder_2_cout;

  half_adder half_adder_1 (.A(A), .B(B), .S(half_adder_1_s), .Cout(half_adder_1_cout));
  half_adder half_adder_2 (.A(half_adder_1_s), .B(Cin), .S(S), .Cout(half_adder_2_cout));
  or or_1 (Cout, half_adder_2_cout, half_adder_1_cout);
endmodule

module Adder_Subtractor_4bit (
  input  [3:0] A,
  input  [3:0] B,
  input  Sign,
  output [3:0] S,
  output Cout,
  output V
);

  wire full_adder_2_cout, full_adder_3_cout, full_adder_4_cout, xor_1_out, xor_2_out, xor_3_out, xor_5_out;

  xor xor_1 (xor_1_out, Sign, B[3]);
  full_adder full_adder_1 (.A(A[3]), .B(xor_1_out), .Cin(full_adder_2_cout), .S(S[3]), .Cout(Cout));
  xor xor_2 (xor_2_out, Sign, B[2]);
  full_adder full_adder_2 (.A(A[2]), .B(xor_2_out), .Cin(full_adder_3_cout), .S(S[2]), .Cout(full_adder_2_cout));
  xor xor_3 (xor_3_out, Sign, B[1]);
  full_adder full_adder_3 (.A(A[1]), .B(xor_3_out), .Cin(full_adder_4_cout), .S(S[1]), .Cout(full_adder_3_cout));
  xor xor_4 (V, full_adder_2_cout, Cout);
  xor xor_5 (xor_5_out, Sign, B[0]);
  full_adder full_adder_4 (.A(A[0]), .B(xor_5_out), .Cin(Sign), .S(S[0]), .Cout(full_adder_4_cout));
endmodule

module ALU (
  input  [2:0] S2S1S0,
  input  [3:0] A,
  input  [3:0] B
);

  wire decoder_1_out0, decoder_1_out1, decoder_1_out2, decoder_1_out3, decoder_1_out4, decoder_1_out5,
       decoder_1_out6, decoder_1_out7, or_2_out;
  wire [3:0] adder_subtractor_4bit_1_s, and_1_out, controlled_buffer_1_out, not_1_out, not_2_out, not_3_out,
       or_1_out, xor_1_out;

  assign and_1_out = A & B;  // AND_Gate and_1, 4 bits wide
  assign or_1_out = A | B;  // OR_Gate or_1, 4 bits wide
  assign xor_1_out = A ^ B;  // XOR_Gate xor_1, 4 bits wide
  assign not_1_out = ~A;  // NOT_Gate not_1, 4 bits wide
  assign not_2_out = ~and_1_out;  // NOT_Gate not_2, 4 bits wide
  Adder_Subtractor_4bit adder_subtractor_4bit_1 (
    .A(A), .B(B), .Sign(decoder_1_out1), .S(adder_subtractor_4bit_1_s));  // open: Cout, V
  assign not_3_out = ~or_1_out;  // NOT_Gate not_3, 4 bits wide
  Decoder #(.select(3)) decoder_1 (
    .out0(decoder_1_out0), .out1(decoder_1_out1), .out2(decoder_1_out2), .out3(decoder_1_out3),
    .out4(decoder_1_out4), .out5(decoder_1_out5), .out6(decoder_1_out6), .out7(decoder_1_out7), .sel(S2S1S0));  // open: en
  or or_2 (or_2_out, decoder_1_out0, decoder_1_out1);
  assign controlled_buffer_1_out = or_2_out ? adder_subtractor_4bit_1_s : 4'bz;  // Controlled_Buffer controlled_buffer_1
  assign controlled_buffer_1_out = decoder_1_out2 ? and_1_out : 4'bz;  // Controlled_Buffer controlled_buffer_2
  assign controlled_buffer_1_out = decoder_1_out3 ? or_1_out : 4'bz;  // Controlled_Buffer controlled_buffer_3
  assign controlled_buffer_1_out = decoder_1_out4 ? xor_1_out : 4'bz;  // Controlled_Buffer controlled_buffer_4
  assign controlled_buffer_1_out = decoder_1_out5 ? not_1_out : 4'bz;  // Controlled_Buffer controlled_buffer_5
  assign controlled_buffer_1_out = decoder_1_out6 ? not_2_out : 4'bz;  // Controlled_Buffer controlled_buffer_6
  assign controlled_buffer_1_out = decoder_1_out7 ? not_3_out : 4'bz;  // Controlled_Buffer controlled_buffer_7
endmodule
