// Logisim project Class_Projects_Jovanf.circ as structural Verilog: 26 circuits, main circuit SOPandNAND
module TODO (
);


  // Notes on the sheet:
  //   MAke demux
endmodule

module SOPandNAND (
  input  in_1,
  input  in_2,
  input  in_3,
  input  in_4,
  input  in_5,
  input  A,
  input  B,
  input  C,
  input  in_9,
  input  in_10,
  output out_11,
  output out_12
);

  wire and_1_out, and_2_out, nand_1_out, nand_2_out, nand_3_out, nand_4_out, not_1_out;

  not not_1 (not_1_out, in_3);
  nand nand_1 (nand_1_out, C, C);
  nand nand_2 (nand_2_out, in_10, in_10);
  and and_1 (and_1_out, in_1, in_2);
  and and_2 (and_2_out, not_1_out, in_4);
  nand nand_3 (nand_3_out, A, B);
  nand nand_4 (nand_4_out, nand_1_out, in_9);
  or or_1 (out_11, and_1_out, and_2_out, in_5);
  nand nand_5 (out_12, nand_3_out, nand_4_out, nand_2_out);

  // Notes on the sheet:
  //   The efficiency of NANDs in a circuit instead of ANDs and ORs lie in real world practice.
endmodule

module POSandNOR (
  input  in_1,
  input  in_2,
  input  in_3,
  input  in_4,
  input  in_5,
  input  in_6,
  input  in_7,
  input  in_8,
  input  in_9,
  input  in_10,
  output out_11,
  output out_12
);

  wire nor_1_out, nor_2_out, nor_3_out, nor_4_out, not_1_out, or_1_out, or_2_out;

  or or_1 (or_1_out, in_1, in_2);
  not not_1 (not_1_out, in_3);
  or or_2 (or_2_out, not_1_out, in_4);
  nor nor_1 (nor_1_out, in_8, in_8);
  nor nor_2 (nor_2_out, in_10, in_10);
  nor nor_3 (nor_3_out, in_6, in_7);
  nor nor_4 (nor_4_out, nor_1_out, in_9);
  and and_1 (out_11, or_1_out, or_2_out, in_5);
  nor nor_5 (out_12, nor_3_out, nor_4_out, nor_2_out);
endmodule

module CONVERT (
  input  IN1,
  input  IN2,
  input  IN3,
  input  IN4,
  output OUT1,
  output OUT2,
  output OUT3,
  output OUT4,
  output out_9,
  output out_10,
  output out_11,
  output out_12
);

  BCDtoEX3 bcdtoex3_1 (.A(IN1), .B(IN2), .C(IN3), .D(IN4), .W(OUT1), .X(OUT2), .Y(OUT3), .Z(OUT4));
  BCDtoEXC3POS bcdtoexc3pos_1 (.A(IN1), .B(IN2), .C(IN3), .D(IN4), .W(out_9), .X(out_10), .Y(out_11), .Z(out_12));

  // Notes on the sheet:
  //   valid inputs: 0000 to 1001
endmodule

module BCDtoEX3 (
  input  A,
  input  B,
  input  C,
  input  D,
  output W,
  output X,
  output Y,
  output Z
);

  wire and_1_out, and_2_out, and_3_out, and_4_out, not_1_out, not_2_out, T1_out;

  or T1 (T1_out, C, D);
  not not_1 (not_1_out, B);
  not not_2 (not_2_out, T1_out);
  not not_3 (Z, D);
  and and_1 (and_1_out, B, T1_out);
  and and_2 (and_2_out, not_1_out, T1_out);
  and and_3 (and_3_out, B, not_2_out);
  and and_4 (and_4_out, C, D);
  or or_1 (W, A, and_1_out);
  or or_2 (X, and_2_out, and_3_out);
  or or_3 (Y, and_4_out, not_2_out);

  // Notes on the sheet:
  //   T = C + D
  //   W = A+BT
  //   X = BT + BT'
  //   Y = CD + T'
  //   Z = D'
endmodule

module BCDtoEXC3POS (
  input  A,
  input  B,
  input  C,
  input  D,
  output W,
  output X,
  output Y,
  output Z
);

  wire nand_1_out, nand_2_out, nand_3_out, nand_4_out, nand_5_out, nand_6_out, nand_8_out, nand_9_out,
       nand_10_out, nand_11_out;

  nand nand_1 (nand_1_out, C, C);
  nand nand_2 (nand_2_out, D, D);
  nand nand_3 (nand_3_out, nand_1_out, nand_2_out);
  nand nand_4 (nand_4_out, A, A);
  nand nand_5 (nand_5_out, B, B);
  nand nand_6 (nand_6_out, nand_3_out, nand_3_out);
  nand nand_7 (Z, D, D);
  nand nand_8 (nand_8_out, B, nand_3_out);
  nand nand_9 (nand_9_out, nand_5_out, nand_3_out);
  nand nand_10 (nand_10_out, B, nand_6_out);
  nand nand_11 (nand_11_out, C, D);
  nand nand_12 (W, nand_4_out, nand_8_out);
  nand nand_13 (X, nand_9_out, nand_10_out);
  nand nand_14 (Y, nand_11_out, nand_3_out);

  // Notes on the sheet:
  //   T = C + D
  //   W = A+BT
  //   X = BT + BT'
  //   Y = CD + T'
  //   Z = D'
endmodule

module Decoder1x2 (
  input  I,
  output O0,
  output O1
);

  not not_1 (O0, I);

  assign O1 = I;
endmodule

module Decoder2x4 (
  input  I0,
  input  I1,
  output O0,
  output O1,
  output O2,
  output O3
);

  wire decoder1x2_1_o0, decoder1x2_1_o1, decoder1x2_2_o0, decoder1x2_2_o1;

  Decoder1x2 decoder1x2_1 (.I(I0), .O0(decoder1x2_1_o0), .O1(decoder1x2_1_o1));
  Decoder1x2 decoder1x2_2 (.I(I1), .O0(decoder1x2_2_o0), .O1(decoder1x2_2_o1));
  and and_1 (O0, decoder1x2_2_o0, decoder1x2_1_o0);
  and and_2 (O1, decoder1x2_2_o0, decoder1x2_1_o1);
  and and_3 (O2, decoder1x2_2_o1, decoder1x2_1_o0);
  and and_4 (O3, decoder1x2_2_o1, decoder1x2_1_o1);
endmodule

module Decoder3x8 (
  input  I2,
  input  I1,
  input  I0,
  output O0,
  output O1,
  output O2,
  output O3,
  output O4,
  output O5,
  output O6,
  output O7
);

  wire decoder1x2_1_o0, decoder1x2_1_o1, decoder2x4_1_o0, decoder2x4_1_o1, decoder2x4_1_o2, decoder2x4_1_o3;

  Decoder2x4 decoder2x4_1 (
    .I0(I0), .I1(I1), .O0(decoder2x4_1_o0), .O1(decoder2x4_1_o1), .O2(decoder2x4_1_o2), .O3(decoder2x4_1_o3));
  Decoder1x2 decoder1x2_1 (.I(I2), .O0(decoder1x2_1_o0), .O1(decoder1x2_1_o1));
  and and_1 (O0, decoder1x2_1_o0, decoder2x4_1_o0);
  and and_2 (O1, decoder1x2_1_o0, decoder2x4_1_o1);
  and and_3 (O2, decoder1x2_1_o0, decoder2x4_1_o2);
  and and_4 (O3, decoder1x2_1_o0, decoder2x4_1_o3);
  and and_5 (O4, decoder1x2_1_o1, decoder2x4_1_o0);
  and and_6 (O5, decoder1x2_1_o1, decoder2x4_1_o1);
  and and_7 (O6, decoder1x2_1_o1, decoder2x4_1_o2);
  and and_8 (O7, decoder1x2_1_o1, decoder2x4_1_o3);
endmodule

module Decoder4x16 (
  input  I0,
  input  I1,
  input  I2,
  input  I3,
  output O0,
  output O1,
  output O2,
  output O3,
  output O4,
  output O5,
  output O6,
  output O7,
  output O8,
  output O9,
  output O10,
  output O11,
  output O12,
  output O13,
  output O14,
  output O15
);

  wire demultiplexer_1_out0, demultiplexer_1_out1, demultiplexer_1_out2, demultiplexer_1_out3;

  Demultiplexer #(.select(2)) demultiplexer_1 (
    .out0(demultiplexer_1_out0), .out1(demultiplexer_1_out1), .out2(demultiplexer_1_out2),
    .out3(demultiplexer_1_out3), .in(1'b1), .sel({I3, I2}));
  Demultiplexer #(.select(2)) demultiplexer_2 (
    .out0(O0), .out1(O1), .out2(O2), .out3(O3), .in(demultiplexer_1_out0), .sel({I1, I0}));
  Demultiplexer #(.select(2)) demultiplexer_3 (
    .out0(O4), .out1(O5), .out2(O6), .out3(O7), .in(demultiplexer_1_out1), .sel({I1, I0}));
  Demultiplexer #(.select(2)) demultiplexer_4 (
    .out0(O8), .out1(O9), .out2(O10), .out3(O11), .in(demultiplexer_1_out2), .sel({I1, I0}));
  Demultiplexer #(.select(2)) demultiplexer_5 (
    .out0(O12), .out1(O13), .out2(O14), .out3(O15), .in(demultiplexer_1_out3), .sel({I1, I0}));
endmodule

module Decoder3to8from2to4and1to2 (
  input  X,
  input  Y,
  input  Z,
  output O0,
  output O1,
  output O2,
  output O3,
  output O4,
  output O5,
  output O6,
  output O7
);

  wire decoder1x2_1_o0, decoder1x2_1_o1, decoder2x4_1_o0, decoder2x4_1_o1, decoder2x4_1_o2, decoder2x4_1_o3;

  Decoder1x2 decoder1x2_1 (.I(X), .O0(decoder1x2_1_o0), .O1(decoder1x2_1_o1));
  Decoder2x4 decoder2x4_1 (
    .I0(Z), .I1(Y), .O0(decoder2x4_1_o0), .O1(decoder2x4_1_o1), .O2(decoder2x4_1_o2), .O3(decoder2x4_1_o3));
  and and_1 (O0, decoder2x4_1_o0, decoder1x2_1_o0);
  and and_2 (O1, decoder2x4_1_o1, decoder1x2_1_o0);
  and and_3 (O2, decoder2x4_1_o2, decoder1x2_1_o0);
  and and_4 (O3, decoder2x4_1_o3, decoder1x2_1_o0);
  and and_5 (O4, decoder2x4_1_o0, decoder1x2_1_o1);
  and and_6 (O5, decoder2x4_1_o1, decoder1x2_1_o1);
  and and_7 (O6, decoder2x4_1_o2, decoder1x2_1_o1);
  and and_8 (O7, decoder2x4_1_o3, decoder1x2_1_o1);
endmodule

module HalfBitAdder (
  input  IN1,
  input  IN2,
  output S,
  output C
);

  xor xor_1 (S, IN1, IN2);
  and and_1 (C, IN1, IN2);
endmodule

module FullBitAdder (
  input  IN1,
  input  IN2,
  input  Cin,
  output S,
  output Cout
);

  wire halfbitadder_1_c, halfbitadder_1_s, halfbitadder_2_c;

  HalfBitAdder halfbitadder_1 (.IN1(IN1), .IN2(IN2), .S(halfbitadder_1_s), .C(halfbitadder_1_c));
  HalfBitAdder halfbitadder_2 (.IN1(halfbitadder_1_s), .IN2(Cin), .S(S), .C(halfbitadder_2_c));
  or or_1 (Cout, halfbitadder_2_c, halfbitadder_1_c);
endmodule

module FourBitAdderSubtractor (
  input  [3:0] A,
  input  [3:0] B,
  input  S,
  output INTOVERFLOW,
  output O3,
  output O2,
  output O1,
  output O0
);

  wire fullbitadder_1_cout, fullbitadder_2_cout, fullbitadder_3_cout, fullbitadder_4_cout, xor_1_out,
       xor_2_out, xor_3_out, xor_4_out;

  xor xor_1 (xor_1_out, B[3], S);
  xor xor_2 (xor_2_out, B[2], S);
  xor xor_3 (xor_3_out, B[1], S);
  xor xor_4 (xor_4_out, B[0], S);
  FullBitAdder fullbitadder_1 (
    .IN1(A[3]), .IN2(xor_1_out), .Cin(fullbitadder_2_cout), .S(O3), .Cout(fullbitadder_1_cout));
  FullBitAdder fullbitadder_2 (
    .IN1(A[2]), .IN2(xor_2_out), .Cin(fullbitadder_3_cout), .S(O2), .Cout(fullbitadder_2_cout));
  FullBitAdder fullbitadder_3 (
    .IN1(A[1]), .IN2(xor_3_out), .Cin(fullbitadder_4_cout), .S(O1), .Cout(fullbitadder_3_cout));
  FullBitAdder fullbitadder_4 (.IN1(A[0]), .IN2(xor_4_out), .Cin(S), .S(O0), .Cout(fullbitadder_4_cout));
  xor xor_5 (INTOVERFLOW, fullbitadder_1_cout, S);

  // Notes on the sheet:
  //   the extra +1
endmodule

module SixteenBitAdder (
  input  [15:0] A,
  input  [15:0] B,
  input  S
);

  FourBitAdderSubtractor fourbitaddersubtractor_1 (.A(A[3:0]), .B(B[3:0]));  // open: S, INTOVERFLOW, O3, O2, O1, O0
  FourBitAdderSubtractor fourbitaddersubtractor_2 (.A(A[7:4]), .B(B[7:4]));  // open: S, INTOVERFLOW, O3, O2, O1, O0
  FourBitAdderSubtractor fourbitaddersubtractor_3 (.A(A[11:8]), .B(B[11:8]));  // open: S, INTOVERFLOW, O3, O2, O1, O0
  FourBitAdderSubtractor fourbitaddersubtractor_4 (.A(A[15:12]), .B(B[15:12]));  // open: S, INTOVERFLOW, O3, O2, O1, O0
endmodule

module Decoder2x4wEnable (
  input  I0,
  input  I1,
  input  E,
  output O0,
  output O1,
  output O2,
  output O3
);

  wire decoder1x2_1_o0, decoder1x2_1_o1, decoder1x2_2_o0, decoder1x2_2_o1;

  Decoder1x2 decoder1x2_1 (.I(I0), .O0(decoder1x2_1_o0), .O1(decoder1x2_1_o1));
  Decoder1x2 decoder1x2_2 (.I(I1), .O0(decoder1x2_2_o0), .O1(decoder1x2_2_o1));
  and and_1 (O0, decoder1x2_2_o0, E, decoder1x2_1_o0);
  and and_2 (O1, decoder1x2_2_o0, E, decoder1x2_1_o1);
  and and_3 (O2, decoder1x2_2_o1, E, decoder1x2_1_o0);
  and and_4 (O3, decoder1x2_2_o1, E, decoder1x2_1_o1);
endmodule

module Decoder3x8from2x4 (
  input  X,
  input  Y,
  input  Z,
  output O0,
  output O1,
  output O2,
  output O3,
  output O4,
  output O5,
  output O6,
  output O7
);

  wire not_1_out;

  not not_1 (not_1_out, X);
  Decoder2x4wEnable decoder2x4wenable_1 (.I0(Z), .I1(Y), .E(not_1_out), .O0(O0), .O1(O1), .O2(O2), .O3(O3));
  Decoder2x4wEnable decoder2x4wenable_2 (.I0(Z), .I1(Y), .E(X), .O0(O4), .O1(O5), .O2(O6), .O3(O7));
endmodule

module FullBitAdderwDecoder (
  input  A,
  input  B,
  input  Cin,
  output SUM,
  output Cout
);

  wire decoder3x8_1_o1, decoder3x8_1_o2, decoder3x8_1_o3, decoder3x8_1_o4, decoder3x8_1_o5, decoder3x8_1_o6,
       decoder3x8_1_o7;

  Decoder3x8 decoder3x8_1 (
    .I2(A), .I1(B), .I0(Cin), .O1(decoder3x8_1_o1), .O2(decoder3x8_1_o2), .O3(decoder3x8_1_o3),
    .O4(decoder3x8_1_o4), .O5(decoder3x8_1_o5), .O6(decoder3x8_1_o6), .O7(decoder3x8_1_o7));  // open: O0
  or or_1 (SUM, decoder3x8_1_o1, decoder3x8_1_o2, decoder3x8_1_o4, decoder3x8_1_o7);
  or or_2 (Cout, decoder3x8_1_o3, decoder3x8_1_o5, decoder3x8_1_o6, decoder3x8_1_o7);
endmodule

module Enc8to3 (
  input  D0,
  input  D1,
  input  D2,
  input  D3,
  input  D4,
  input  D5,
  input  D6,
  input  D7,
  output B2,
  output B1,
  output B0
);

  or or_1 (B2, D7, D6, D5, D4);
  or or_2 (B1, D7, D6, D3, D2);
  or or_3 (B0, D7, D5, D3, D1);
endmodule

module Mux4to1 (
  input  S1,
  input  S0,
  input  I0,
  input  I1,
  input  I2,
  input  I3,
  output out_7
);

  wire and_1_out, and_2_out, and_3_out, and_4_out, decoder2x4_1_o0, decoder2x4_1_o1, decoder2x4_1_o2,
       decoder2x4_1_o3;

  Decoder2x4 decoder2x4_1 (
    .I0(S0), .I1(S1), .O0(decoder2x4_1_o0), .O1(decoder2x4_1_o1), .O2(decoder2x4_1_o2), .O3(decoder2x4_1_o3));
  and and_1 (and_1_out, decoder2x4_1_o0, I0);
  and and_2 (and_2_out, decoder2x4_1_o1, I1);
  and and_3 (and_3_out, decoder2x4_1_o2, I2);
  and and_4 (and_4_out, decoder2x4_1_o3, I3);
  or or_1 (out_7, and_1_out, and_2_out, and_3_out, and_4_out);

  // Notes on the sheet:
  //   Purpose: select which data goes through
endmodule

module PrEnc4to2 (
  input  M3,
  input  M2,
  input  M1,
  input  M0,
  output V,
  output O1,
  output O0
);

  wire and_1_out, not_1_out;

  not not_1 (not_1_out, M2);
  and and_1 (and_1_out, not_1_out, M1);
  or or_1 (V, M3, M2, M1, M0);
  or or_2 (O1, M2, M3);
  or or_3 (O0, and_1_out, M3);
endmodule

module GraytoBinMUX8to1 (
  input  A,
  input  B,
  input  C,
  output X,
  output Y,
  output Z
);

  Multiplexer #(.select(3)) multiplexer_1 (
    .in0(1'b0), .in1(1'b0), .in2(1'b1), .in3(1'b1), .in4(1'b1), .in5(1'b1), .in6(1'b0), .in7(1'b0), .out(Y),
    .sel({A, B, C}));
  Multiplexer #(.select(3)) multiplexer_2 (
    .in0(1'b0), .in1(1'b1), .in2(1'b1), .in3(1'b0), .in4(1'b1), .in5(1'b0), .in6(1'b0), .in7(1'b1), .out(Z),
    .sel({A, B, C}));

  assign X = A;
endmodule

module GraytoBinDecoder (
  input  [2:0] in_1,
  output [2:0] out_2
);

  wire decoder3x8_1_o1, decoder3x8_1_o2, decoder3x8_1_o3, decoder3x8_1_o4, decoder3x8_1_o5, decoder3x8_1_o6,
       decoder3x8_1_o7;

  Decoder3x8 decoder3x8_1 (
    .I2(in_1[2]), .I1(in_1[1]), .I0(in_1[0]), .O1(decoder3x8_1_o1), .O2(decoder3x8_1_o2),
    .O3(decoder3x8_1_o3), .O4(decoder3x8_1_o4), .O5(decoder3x8_1_o5), .O6(decoder3x8_1_o6),
    .O7(decoder3x8_1_o7));  // open: O0
  or or_1 (out_2[2], decoder3x8_1_o4, decoder3x8_1_o5, decoder3x8_1_o6, decoder3x8_1_o7);
  or or_2 (out_2[1], decoder3x8_1_o2, decoder3x8_1_o3, decoder3x8_1_o4, decoder3x8_1_o5);
  or or_3 (out_2[0], decoder3x8_1_o1, decoder3x8_1_o2, decoder3x8_1_o4, decoder3x8_1_o7);
endmodule

module GraytoBinKMap (
  input  A,
  input  B,
  input  C,
  output X,
  output Y,
  output Z
);


  assign X = A;

  // Notes on the sheet:
  //   MALAS
endmodule

module Mux8to1w (
  input  in_1
);
endmodule

module SoalwDecoder (
  input  A,
  input  B,
  input  C,
  input  D,
  output F
);

  wire decoder4x16_1_o1, decoder4x16_1_o3, decoder4x16_1_o4, decoder4x16_1_o5, decoder4x16_1_o6;

  Decoder4x16 decoder4x16_1 (
    .I0(A), .I1(B), .I2(C), .I3(D), .O1(decoder4x16_1_o1), .O3(decoder4x16_1_o3), .O4(decoder4x16_1_o4),
    .O5(decoder4x16_1_o5), .O6(decoder4x16_1_o6));  // open: O0, O2, O7, O8, O9, O10, O11, O12, O13, O14, O15
  or or_1 (F, decoder4x16_1_o1, decoder4x16_1_o3, decoder4x16_1_o4, decoder4x16_1_o5, decoder4x16_1_o6);

  // Notes on the sheet:
  //   udah tau intinya
endmodule
