// Logisim project MedsDispenser.circ as structural Verilog
module main (
);


  // Notes on the sheet:
  //       Allows medication only at prescribed times (e.g., every 8 hours)     Locks after dispensing to prevent overdosing     Shows next available time on a display     Provides visual/auditory alerts when medication is due     Has an emergency override for medical emergencies
endmodule

module Counter4bitWithLimit (
  input  [3:0] T,
  input  CountE,
  input  CLK,
  output [3:0] O,
  output COut
);

  wire and_1_out, and_2_out, and_3_out, and_5_out;
  wire [3:0] xnor_1_out, xor_1_out;

  and and_1 (and_1_out, CountE, O[0]);
  and and_2 (and_2_out, and_1_out, O[1]);
  and and_3 (and_3_out, and_2_out, O[2]);
  // AND_Gate and_4 has open pins: in0=and_3_out, in1=O[3], out=open
  assign xnor_1_out = ~(T ^ O);  // XNOR_Gate xnor_1, 4 bits wide
  xor xor_1 (xor_1_out[0], O[0], CountE);
  xor xor_2 (xor_1_out[1], O[1], and_1_out);
  xor xor_3 (xor_1_out[2], O[2], and_2_out);
  xor xor_4 (xor_1_out[3], O[3], and_3_out);
  and and_5 (and_5_out, xnor_1_out[0], xnor_1_out[1], xnor_1_out[2], xnor_1_out[3]);
  D_Flip_Flop d_ff_1 (.D(and_5_out), .clk(CLK), .Q(COut));  // open: Qn, preset, reset
  Register4bit register4bit_1 (.I(xor_1_out), .WE(CountE), .RE(1'b1), .R(COut), .CLK(CLK), .O(O));
endmodule

module DFlipFlopNegEdge (
  input  D,
  input  CLK,
  input  R,
  output Q,
  output Qn
);

  wire and_1_out, clockedsrlatch_1_q, clockedsrlatch_1_qn, not_1_out, not_2_out, not_3_out;

  not not_1 (not_1_out, R);
  and and_1 (and_1_out, D, not_1_out);
  not not_2 (not_2_out, and_1_out);
  ClockedSRLatch clockedsrlatch_1 (
    .S(and_1_out), .R(not_2_out), .CLK(CLK), .Q(clockedsrlatch_1_q), .Qn(clockedsrlatch_1_qn));
  not not_3 (not_3_out, CLK);
  ClockedSRLatch clockedsrlatch_2 (.S(clockedsrlatch_1_q), .R(clockedsrlatch_1_qn), .CLK(not_3_out), .Q(Q), .Qn(Qn));
endmodule

module ClockedSRLatch (
  input  S,
  input  R,
  input  CLK,
  output Q,
  output Qn
);

  wire nand_1_out, nand_2_out;

  nand nand_1 (nand_1_out, S, CLK);
  nand nand_2 (nand_2_out, CLK, R);
  nand nand_3 (Q, nand_1_out, Qn);
  nand nand_4 (Qn, Q, nand_2_out);
endmodule

module Register4bit (
  input  [3:0] I,
  input  WE,
  input  RE,
  input  R,
  input  CLK,
  output [3:0] O
);

  wire and_1_out;
  wire [3:0] d_ff_1_q;

  D_Flip_Flop d_ff_1 (.D(I[0]), .clk(and_1_out), .Q(d_ff_1_q[0]), .reset(R));  // open: Qn, preset
  D_Flip_Flop d_ff_2 (.D(I[1]), .clk(and_1_out), .Q(d_ff_1_q[1]), .reset(R));  // open: Qn, preset
  D_Flip_Flop d_ff_3 (.D(I[2]), .clk(and_1_out), .Q(d_ff_1_q[2]), .reset(R));  // open: Qn, preset
  D_Flip_Flop d_ff_4 (.D(I[3]), .clk(and_1_out), .Q(d_ff_1_q[3]), .reset(R));  // open: Qn, preset
  and and_1 (and_1_out, WE, CLK);
  assign O = RE ? d_ff_1_q : 4'bz;  // Controlled_Buffer controlled_buffer_1

  // Notes on the sheet:
  //   dis one is pipo
endmodule

module JKFlipFlop (
  input  J,
  input  K,
  input  CLK,
  output Q,
  output Qn
);

  wire and_1_out, and_2_out;

  and and_1 (and_1_out, J, Qn);
  and and_2 (and_2_out, Q, K);
  ClockedSRLatch clockedsrlatch_1 (.S(and_1_out), .R(and_2_out), .CLK(CLK), .Q(Q), .Qn(Qn));

  // Notes on the sheet:
  //   ...some other time.
endmodule

module CounterSeveralDigits (
  input  [3:0] T,
  input  CountE
);

  wire CLK_out, counter4bitwithlimit_1_cout, counter4bitwithlimit_2_cout;
  wire [3:0] counter4bitwithlimit_1_o, counter4bitwithlimit_2_o, counter4bitwithlimit_3_o;

  Clock CLK (.out(CLK_out));
  Hex_Digit_Display hex_digit_display_1 (.value(counter4bitwithlimit_3_o));  // open: dp
  Counter4bitWithLimit counter4bitwithlimit_1 (
    .T(T), .CountE(CountE), .CLK(CLK_out), .O(counter4bitwithlimit_1_o), .COut(counter4bitwithlimit_1_cout));
  Counter4bitWithLimit counter4bitwithlimit_2 (
    .T(T), .CountE(CountE), .CLK(counter4bitwithlimit_1_cout), .O(counter4bitwithlimit_2_o),
    .COut(counter4bitwithlimit_2_cout));
  Counter4bitWithLimit counter4bitwithlimit_3 (
    .T(T), .CountE(CountE), .CLK(counter4bitwithlimit_2_cout), .O(counter4bitwithlimit_3_o));  // open: COut
  Hex_Digit_Display hex_digit_display_2 (.value(counter4bitwithlimit_2_o));  // open: dp
  Hex_Digit_Display hex_digit_display_3 (.value(counter4bitwithlimit_1_o));  // open: dp
endmodule

module RAMCell (
  input  S,
  input  D,
  input  Dc,
  input  CLK,
  output O,
  output Oc
);

  wire and_1_out, and_2_out, s_r_ff_1_q, s_r_ff_1_qn;

  and and_1 (and_1_out, D, S);
  S_R_Flip_Flop s_r_ff_1 (
    .S(and_1_out), .R(and_2_out), .clk(CLK), .Q(s_r_ff_1_q), .Qn(s_r_ff_1_qn));  // open: reset, preset
  and and_2 (and_2_out, S, Dc);
  and and_3 (O, S, s_r_ff_1_q);
  and and_4 (Oc, S, s_r_ff_1_qn);

  // Notes on the sheet:
  //   if no S: cant write, output 0 0.
endmodule

module RAMBitSlice_4bits (
  input  [1:0] Addr,
  input  DataIn,
  input  WE,
  input  ChipSelect,
  input  CLK,
  output O
);

  wire and_1_out, and_2_out, and_3_out, and_4_out, decoder_1_out0, decoder_1_out1, decoder_1_out2,
       decoder_1_out3, not_1_out, not_2_out, or_1_out, ramcell_1_o, ramcell_2_o, ramcell_3_o, ramcell_4_o;

  Decoder #(.select(2)) decoder_1 (
    .out0(decoder_1_out0), .out1(decoder_1_out1), .out2(decoder_1_out2), .out3(decoder_1_out3), .sel(Addr));  // open: en
  and and_1 (and_1_out, and_2_out, DataIn);
  and and_2 (and_2_out, WE, ChipSelect);
  not not_1 (not_1_out, WE);
  and and_3 (and_3_out, and_2_out, not_2_out);
  not not_2 (not_2_out, DataIn);
  RAMCell ramcell_1 (.S(decoder_1_out0), .D(and_1_out), .Dc(and_3_out), .CLK(CLK), .O(ramcell_1_o));  // open: Oc
  RAMCell ramcell_2 (.S(decoder_1_out1), .D(and_1_out), .Dc(and_3_out), .CLK(CLK), .O(ramcell_2_o));  // open: Oc
  RAMCell ramcell_3 (.S(decoder_1_out2), .D(and_1_out), .Dc(and_3_out), .CLK(CLK), .O(ramcell_3_o));  // open: Oc
  RAMCell ramcell_4 (.S(decoder_1_out3), .D(and_1_out), .Dc(and_3_out), .CLK(CLK), .O(ramcell_4_o));  // open: Oc
  or or_1 (or_1_out, ramcell_4_o, ramcell_3_o, ramcell_2_o, ramcell_1_o);
  and and_4 (and_4_out, not_1_out, ChipSelect);
  assign O = and_4_out ? or_1_out : 1'bz;  // Controlled_Buffer controlled_buffer_1

  // Notes on the sheet:
  //   decoder can use chip select as en
  //   A bit slice represents bit-n of ALL addresses!
  //   first one to represent bit 0, second represents bit 1, and so on.
  //   a 4x16 RAM chip uses 16 4 bit slices.
  //   so for example, 4 bit slices can be used for 4 addresses (can be more)
  //   TLDR example: bit slice contains 4 bits -> there are 4 addresses
  //   + that means this is always on, one of these is selected (but why do we need to select which bits)
  //   to join the several outputs, an OR is needed (no output is U yet)
  //   output wont show if the bit aint selected
  //   in logisim's builtin ram, read only enables the changing of the output
  //   but it seems, in real cases, READ = 0 will make output Hi-Z. so fuck it
  //   READ can be either clocked or free (diff of Sync SRAM vs Async SRAM). in this case i just use Async, but if used, just use a D or SR Flip-flop
  //   so for example if output was (data before) , it will be (data right now) if read is on but if its off, after switching to the next address, the output wont change
endmodule

module RAM4x8Chip (
  input  [1:0] Addr,
  input  [7:0] DataIn,
  input  WE,
  input  ChipSelect,
  input  CLK,
  output [7:0] O
);

  RAMBitSlice_4bits rambitslice_4bits_1 (
    .Addr(Addr), .DataIn(DataIn[0]), .WE(WE), .ChipSelect(ChipSelect), .CLK(CLK), .O(O[0]));
  RAMBitSlice_4bits rambitslice_4bits_2 (
    .Addr(Addr), .DataIn(DataIn[1]), .WE(WE), .ChipSelect(ChipSelect), .CLK(CLK), .O(O[1]));
  RAMBitSlice_4bits rambitslice_4bits_3 (
    .Addr(Addr), .DataIn(DataIn[2]), .WE(WE), .ChipSelect(ChipSelect), .CLK(CLK), .O(O[2]));
  RAMBitSlice_4bits rambitslice_4bits_4 (
    .Addr(Addr), .DataIn(DataIn[3]), .WE(WE), .ChipSelect(ChipSelect), .CLK(CLK), .O(O[3]));
  RAMBitSlice_4bits rambitslice_4bits_5 (
    .Addr(Addr), .DataIn(DataIn[4]), .WE(WE), .ChipSelect(ChipSelect), .CLK(CLK), .O(O[4]));
  RAMBitSlice_4bits rambitslice_4bits_6 (
    .Addr(Addr), .DataIn(DataIn[5]), .WE(WE), .ChipSelect(ChipSelect), .CLK(CLK), .O(O[5]));
  RAMBitSlice_4bits rambitslice_4bits_7 (
    .Addr(Addr), .DataIn(DataIn[6]), .WE(WE), .ChipSelect(ChipSelect), .CLK(CLK), .O(O[6]));
  RAMBitSlice_4bits rambitslice_4bits_8 (
    .Addr(Addr), .DataIn(DataIn[7]), .WE(WE), .ChipSelect(ChipSelect), .CLK(CLK), .O(O[7]));

  // Notes on the sheet:
  //   (assuming 8 means the word length and there are 4 addresses)
  //   this can be considered a memory array (just below bank<-chip<-RAM Module)
endmodule

module Literally_64MB_RAM (
);

  RAM #(.addrWidth(24), .dataWidth(32)) ram_1 ();  // open: addr, we, oe, clk, din, dout
endmodule

module RAM128Kx16_w_64Kx8 (
  input  [16:0] Addr,
  input  ChipSelect,
  input  WE,
  input  RE,
  input  [15:0] DataIn,
  input  CLK,
  output [15:0] O
);

  wire and_1_out, and_2_out, and_3_out, and_4_out, and_5_out, and_6_out, not_1_out;
  wire [7:0] ram_1_dout, ram_2_dout, ram_3_dout, ram_4_dout;

  not not_1 (not_1_out, Addr[16]);
  and and_1 (and_1_out, not_1_out, ChipSelect);
  and and_2 (and_2_out, and_1_out, RE);
  and and_3 (and_3_out, RE, and_4_out);
  and and_4 (and_4_out, Addr[16], ChipSelect);
  and and_5 (and_5_out, and_1_out, WE);
  and and_6 (and_6_out, WE, and_4_out);
  RAM #(.addrWidth(16)) ram_1 (
    .addr(Addr[15:0]), .we(and_5_out), .oe(and_2_out), .clk(CLK), .din(DataIn[7:0]), .dout(ram_1_dout));
  RAM #(.addrWidth(16)) ram_2 (
    .addr(Addr[15:0]), .we(and_6_out), .oe(and_3_out), .clk(CLK), .din(DataIn[7:0]), .dout(ram_2_dout));
  RAM #(.addrWidth(16)) ram_3 (
    .addr(Addr[15:0]), .we(and_5_out), .oe(and_2_out), .clk(CLK), .din(DataIn[15:8]), .dout(ram_3_dout));
  RAM #(.addrWidth(16)) ram_4 (
    .addr(Addr[15:0]), .we(and_6_out), .oe(and_3_out), .clk(CLK), .din(DataIn[15:8]), .dout(ram_4_dout));
  assign O = and_3_out ? {ram_4_dout, ram_2_dout} : 16'bz;  // Controlled_Buffer controlled_buffer_1
  assign O = and_2_out ? {ram_3_dout, ram_1_dout} : 16'bz;  // Controlled_Buffer controlled_buffer_2

  // Notes on the sheet:
  //   somehow succeeded with all this spagghetti
endmodule

module OmniShiftPIPO4bit (
  input  [1:0] Mode,
  input  [3:0] DataIn,
  input  Fill,
  input  CLK
);

  wire D0_q, D1_q, D2_q, D3_q, multiplexer_1_out, multiplexer_2_out, multiplexer_3_out, multiplexer_4_out;

  D_Flip_Flop D0 (.D(multiplexer_1_out), .clk(CLK), .Q(D0_q));  // open: Qn, preset, reset
  Multiplexer #(.select(2)) multiplexer_1 (
    .in0(D0_q), .in1(DataIn[0]), .in2(Fill), .in3(D1_q), .out(multiplexer_1_out), .sel(Mode));
  D_Flip_Flop D1 (.D(multiplexer_2_out), .clk(CLK), .Q(D1_q));  // open: Qn, preset, reset
  Multiplexer #(.select(2)) multiplexer_2 (
    .in0(D1_q), .in1(DataIn[1]), .in2(D0_q), .in3(D2_q), .out(multiplexer_2_out), .sel(Mode));
  D_Flip_Flop D2 (.D(multiplexer_3_out), .clk(CLK), .Q(D2_q));  // open: Qn, preset, reset
  Multiplexer #(.select(2)) multiplexer_3 (
    .in0(D2_q), .in1(DataIn[2]), .in2(D1_q), .in3(D3_q), .out(multiplexer_3_out), .sel(Mode));
  D_Flip_Flop D3 (.D(multiplexer_4_out), .clk(CLK), .Q(D3_q));  // open: Qn, preset, reset
  Multiplexer #(.select(2)) multiplexer_4 (
    .in0(D3_q), .in1(DataIn[3]), .in2(D2_q), .in3(Fill), .out(multiplexer_4_out), .sel(Mode));

  // Notes on the sheet:
  //   00=do nothing, 01=insert new data, 10=SL, 11 = SR
  //   down
  //   up
endmodule
