// Logisim project MemoryCircuits.circ as structural Verilog: 9 circuits, main circuit RAMCell1bit
module RAMCell1bit (
  input  S,
  input  B,
  input  Bn,
  input  CLK,
  output C,
  output Cn,
  output Q
);

  wire and_1_out, and_2_out, s_r_ff_1_qn;

  and and_1 (and_1_out, B, S);
  and and_2 (and_2_out, S, Bn);
  S_R_Flip_Flop #(.trigger("high")) s_r_ff_1 (
    .S(and_1_out), .R(and_2_out), .clk(CLK), .Q(Q), .Qn(s_r_ff_1_qn));  // open: reset, preset
  and and_3 (C, S, Q);
  and and_4 (Cn, S, s_r_ff_1_qn);
endmodule

module RAM4bitRow (
  input  WS0,
  input  WS1,
  input  WS2,
  input  WS3,
  input  DataIn,
  input  WR,
  input  BitSelect,
  input  CLK,
  output Q0,
  output Q1,
  output Q2,
  output Q3,
  output DataOut
);

  wire and_1_out, and_2_out, and_3_out, not_1_out, not_2_out, or_1_out, or_2_out, ramcell1bit_1_c,
       ramcell1bit_1_cn, ramcell1bit_2_c, ramcell1bit_2_cn, ramcell1bit_3_c, ramcell1bit_3_cn,
       ramcell1bit_4_c, ramcell1bit_4_cn, s_r_ff_1_q;

  and and_1 (and_1_out, DataIn, and_2_out);
  and and_2 (and_2_out, not_1_out, BitSelect);
  not not_1 (not_1_out, WR);
  and and_3 (and_3_out, and_2_out, not_2_out);
  not not_2 (not_2_out, DataIn);
  RAMCell1bit ramcell1bit_1 (
    .S(WS0), .B(and_1_out), .Bn(and_3_out), .CLK(CLK), .C(ramcell1bit_1_c), .Cn(ramcell1bit_1_cn), .Q(Q0));
  RAMCell1bit ramcell1bit_2 (
    .S(WS1), .B(and_1_out), .Bn(and_3_out), .CLK(CLK), .C(ramcell1bit_2_c), .Cn(ramcell1bit_2_cn), .Q(Q1));
  RAMCell1bit ramcell1bit_3 (
    .S(WS2), .B(and_1_out), .Bn(and_3_out), .CLK(CLK), .C(ramcell1bit_3_c), .Cn(ramcell1bit_3_cn), .Q(Q2));
  RAMCell1bit ramcell1bit_4 (
    .S(WS3), .B(and_1_out), .Bn(and_3_out), .CLK(CLK), .C(ramcell1bit_4_c), .Cn(ramcell1bit_4_cn), .Q(Q3));
  or or_1 (or_1_out, ramcell1bit_1_c, ramcell1bit_2_c, ramcell1bit_3_c, ramcell1bit_4_c);
  or or_2 (or_2_out, ramcell1bit_1_cn, ramcell1bit_2_cn, ramcell1bit_3_cn, ramcell1bit_4_cn);
  S_R_Flip_Flop #(.trigger("high")) s_r_ff_1 (
    .S(or_1_out), .R(or_2_out), .clk(CLK), .Q(s_r_ff_1_q));  // open: reset, Qn, preset
  assign DataOut = BitSelect ? s_r_ff_1_q : 1'bz;  // Controlled_Buffer controlled_buffer_1

  // Notes on the sheet:
  //   also known as "1 cell split"
  //   ... i think i misread slice as split somehow
endmodule

module RAM16x1_4by4 (
  input  [3:0] S,
  input  DataIn,
  input  WR,
  input  ChipSelect,
  output DataOut
);

  wire CLK_out, decoder_1_out0, decoder_1_out1, decoder_1_out2, decoder_1_out3, decoder_1_out4,
       decoder_1_out5, decoder_1_out6, decoder_1_out7, decoder_1_out8, decoder_1_out9, decoder_1_out10,
       decoder_1_out11, decoder_1_out12, decoder_1_out14, decoder_1_out15, or_1_out, ram4bitrow_1_dataout,
       ram4bitrow_1_q0, ram4bitrow_1_q1, ram4bitrow_1_q2, ram4bitrow_1_q3, ram4bitrow_2_dataout,
       ram4bitrow_2_q0, ram4bitrow_2_q1, ram4bitrow_2_q2, ram4bitrow_2_q3, ram4bitrow_3_dataout,
       ram4bitrow_3_q0, ram4bitrow_3_q1, ram4bitrow_3_q2, ram4bitrow_3_q3, ram4bitrow_4_dataout,
       ram4bitrow_4_q0, ram4bitrow_4_q1, ram4bitrow_4_q2, ram4bitrow_4_q3;

  Clock CLK (.out(CLK_out));
  Decoder #(.select(4)) decoder_1 (
    .out0(decoder_1_out0), .out1(decoder_1_out1), .out2(decoder_1_out2), .out3(decoder_1_out3),
    .out4(decoder_1_out4), .out5(decoder_1_out5), .out6(decoder_1_out6), .out7(decoder_1_out7),
    .out8(decoder_1_out8), .out9(decoder_1_out9), .out10(decoder_1_out10), .out11(decoder_1_out11),
    .out12(decoder_1_out12), .out13(decoder_1_out12), .out14(decoder_1_out14), .out15(decoder_1_out15),
    .sel(S));  // open: en
  LED led_1 (.in(ram4bitrow_1_q0));
  RAM4bitRow ram4bitrow_1 (
    .WS0(decoder_1_out0), .WS1(decoder_1_out1), .WS2(decoder_1_out2), .WS3(decoder_1_out3), .DataIn(DataIn),
    .WR(WR), .BitSelect(ChipSelect), .CLK(CLK_out), .Q0(ram4bitrow_1_q0), .Q1(ram4bitrow_1_q1),
    .Q2(ram4bitrow_1_q2), .Q3(ram4bitrow_1_q3), .DataOut(ram4bitrow_1_dataout));
  LED led_2 (.in(ram4bitrow_1_q1));
  LED led_3 (.in(ram4bitrow_1_q2));
  LED led_4 (.in(ram4bitrow_1_q3));
  LED led_5 (.in(ram4bitrow_2_q0));
  RAM4bitRow ram4bitrow_2 (
    .WS0(decoder_1_out4), .WS1(decoder_1_out5), .WS2(decoder_1_out6), .WS3(decoder_1_out7), .DataIn(DataIn),
    .WR(WR), .BitSelect(ChipSelect), .CLK(CLK_out), .Q0(ram4bitrow_2_q0), .Q1(ram4bitrow_2_q1),
    .Q2(ram4bitrow_2_q2), .Q3(ram4bitrow_2_q3), .DataOut(ram4bitrow_2_dataout));
  LED led_6 (.in(ram4bitrow_2_q1));
  LED led_7 (.in(ram4bitrow_2_q2));
  LED led_8 (.in(ram4bitrow_2_q3));
  LED led_9 (.in(ram4bitrow_3_q0));
  RAM4bitRow ram4bitrow_3 (
    .WS0(decoder_1_out8), .WS1(decoder_1_out9), .WS2(decoder_1_out10), .WS3(decoder_1_out11),
    .DataIn(DataIn), .WR(WR), .BitSelect(ChipSelect), .CLK(CLK_out), .Q0(ram4bitrow_3_q0),
    .Q1(ram4bitrow_3_q1), .Q2(ram4bitrow_3_q2), .Q3(ram4bitrow_3_q3), .DataOut(ram4bitrow_3_dataout));
  LED led_10 (.in(ram4bitrow_3_q1));
  LED led_11 (.in(ram4bitrow_3_q2));
  LED led_12 (.in(ram4bitrow_3_q3));
  LED led_13 (.in(ram4bitrow_4_q0));
  RAM4bitRow ram4bitrow_4 (
    .WS0(decoder_1_out12), .WS1(decoder_1_out12), .WS2(decoder_1_out14), .WS3(decoder_1_out15),
    .DataIn(DataIn), .WR(WR), .BitSelect(ChipSelect), .CLK(CLK_out), .Q0(ram4bitrow_4_q0),
    .Q1(ram4bitrow_4_q1), .Q2(ram4bitrow_4_q2), .Q3(ram4bitrow_4_q3), .DataOut(ram4bitrow_4_dataout));
  LED led_14 (.in(ram4bitrow_4_q1));
  LED led_15 (.in(ram4bitrow_4_q2));
  LED led_16 (.in(ram4bitrow_4_q3));
  or or_1 (or_1_out, ram4bitrow_1_dataout, ram4bitrow_2_dataout, ram4bitrow_3_dataout, ram4bitrow_4_dataout);
  assign DataOut = ChipSelect ? or_1_out : 1'bz;  // Controlled_Buffer controlled_buffer_1

  // Notes on the sheet:
  //   this might be very misleading in how bit slices work
  //   consult "meds dispenser"
endmodule

module RAM8x2_4by4 (
  input  [1:0] A2A1,
  input  A0,
  input  Read,
  input  DataIn0,
  input  DataIn1,
  input  ChipSelect,
  output DataOut0,
  output DataOut1
);

  wire CLK_out, decoder_1_out0, decoder_1_out1, decoder_1_out2, decoder_1_out3, decoder_2_out0,
       decoder_2_out1;

  Decoder #(.select(2)) decoder_1 (
    .out0(decoder_1_out0), .out1(decoder_1_out1), .out2(decoder_1_out2), .out3(decoder_1_out3), .sel(A2A1));  // open: en
  Clock CLK (.out(CLK_out));
  Decoder decoder_2 (.out0(decoder_2_out0), .out1(decoder_2_out1), .sel(A0), .en(ChipSelect));
  RAM4bitRow O0 (
    .WS0(decoder_1_out0), .WS1(decoder_1_out1), .WS2(decoder_1_out2), .WS3(decoder_1_out3), .DataIn(DataIn0),
    .WR(Read), .BitSelect(decoder_2_out0), .CLK(CLK_out), .DataOut(DataOut0));  // open: Q0, Q1, Q2, Q3
  RAM4bitRow O1 (
    .WS0(decoder_1_out0), .WS1(decoder_1_out1), .WS2(decoder_1_out2), .WS3(decoder_1_out3), .DataIn(DataIn1),
    .WR(Read), .BitSelect(decoder_2_out0), .CLK(CLK_out), .DataOut(DataOut1));  // open: Q0, Q1, Q2, Q3
  RAM4bitRow O2 (
    .WS0(decoder_1_out0), .WS1(decoder_1_out1), .WS2(decoder_1_out2), .WS3(decoder_1_out3), .DataIn(DataIn0),
    .WR(Read), .BitSelect(decoder_2_out1), .CLK(CLK_out), .DataOut(DataOut0));  // open: Q0, Q1, Q2, Q3
  RAM4bitRow O3 (
    .WS0(decoder_1_out0), .WS1(decoder_1_out1), .WS2(decoder_1_out2), .WS3(decoder_1_out3), .DataIn(DataIn1),
    .WR(Read), .BitSelect(decoder_2_out1), .CLK(CLK_out), .DataOut(DataOut1));  // open: Q0, Q1, Q2, Q3
endmodule

module RAM4x4_4by4 (
  input  [1:0] A1A0,
  input  Read,
  input  [3:0] DataIn,
  input  ChipSelect,
  output [3:0] DataOut
);

  wire CLK_out, decoder_1_out0, decoder_1_out1, decoder_1_out2, decoder_1_out3;

  Decoder #(.select(2)) decoder_1 (
    .out0(decoder_1_out0), .out1(decoder_1_out1), .out2(decoder_1_out2), .out3(decoder_1_out3), .sel(A1A0));  // open: en
  Clock CLK (.out(CLK_out));
  RAM4bitRow O0 (
    .WS0(decoder_1_out0), .WS1(decoder_1_out1), .WS2(decoder_1_out2), .WS3(decoder_1_out3),
    .DataIn(DataIn[0]), .WR(Read), .BitSelect(ChipSelect), .CLK(CLK_out), .DataOut(DataOut[0]));  // open: Q0, Q1, Q2, Q3
  RAM4bitRow O1 (
    .WS0(decoder_1_out0), .WS1(decoder_1_out1), .WS2(decoder_1_out2), .WS3(decoder_1_out3),
    .DataIn(DataIn[1]), .WR(Read), .BitSelect(ChipSelect), .CLK(CLK_out), .DataOut(DataOut[1]));  // open: Q0, Q1, Q2, Q3
  RAM4bitRow O2 (
    .WS0(decoder_1_out0), .WS1(decoder_1_out1), .WS2(decoder_1_out2), .WS3(decoder_1_out3),
    .DataIn(DataIn[2]), .WR(Read), .BitSelect(ChipSelect), .CLK(CLK_out), .DataOut(DataOut[2]));  // open: Q0, Q1, Q2, Q3
  RAM4bitRow O3 (
    .WS0(decoder_1_out0), .WS1(decoder_1_out1), .WS2(decoder_1_out2), .WS3(decoder_1_out3),
    .DataIn(DataIn[3]), .WR(Read), .BitSelect(ChipSelect), .CLK(CLK_out), .DataOut(DataOut[3]));  // open: Q0, Q1, Q2, Q3
endmodule

module RAM64Kx8 (
  input  [15:0] S,
  input  WriteEn,
  input  ReadEn,
  input  [7:0] DataIn,
  input  CLK,
  output [7:0] DataOut
);

  RAM #(.addrWidth(16)) ram_1 (.addr(S), .we(WriteEn), .oe(ReadEn), .clk(CLK), .din(DataIn), .dout(DataOut));
endmodule

module RAM256Kx8 (
  input  [17:0] S,
  input  WriteEn,
  input  ReadEn,
  input  [7:0] DataIn,
  input  CS,
  input  CLK,
  output [7:0] out_7
);

  wire decoder_1_out0, decoder_1_out1, decoder_1_out2, decoder_1_out3;
  wire [15:0] controlled_buffer_1_out, controlled_buffer_2_out, controlled_buffer_3_out,
       controlled_buffer_4_out;

  Decoder #(.select(2)) decoder_1 (
    .out0(decoder_1_out0), .out1(decoder_1_out1), .out2(decoder_1_out2), .out3(decoder_1_out3),
    .sel(S[17:16]), .en(CS));
  assign controlled_buffer_1_out = decoder_1_out0 ? S[15:0] : 16'bz;  // Controlled_Buffer controlled_buffer_1
  assign controlled_buffer_2_out = decoder_1_out1 ? S[15:0] : 16'bz;  // Controlled_Buffer controlled_buffer_2
  assign controlled_buffer_3_out = decoder_1_out2 ? S[15:0] : 16'bz;  // Controlled_Buffer controlled_buffer_3
  assign controlled_buffer_4_out = decoder_1_out3 ? S[15:0] : 16'bz;  // Controlled_Buffer controlled_buffer_4
  RAM64Kx8 ram64kx8_1 (
    .S(controlled_buffer_1_out), .WriteEn(WriteEn), .ReadEn(ReadEn), .DataIn(DataIn), .CLK(CLK),
    .DataOut(out_7));
  RAM64Kx8 ram64kx8_2 (
    .S(controlled_buffer_2_out), .WriteEn(WriteEn), .ReadEn(ReadEn), .DataIn(DataIn), .CLK(CLK),
    .DataOut(out_7));
  RAM64Kx8 ram64kx8_3 (
    .S(controlled_buffer_3_out), .WriteEn(WriteEn), .ReadEn(ReadEn), .DataIn(DataIn), .CLK(CLK),
    .DataOut(out_7));
  RAM64Kx8 ram64kx8_4 (
    .S(controlled_buffer_4_out), .WriteEn(WriteEn), .ReadEn(ReadEn), .DataIn(DataIn), .CLK(CLK),
    .DataOut(out_7));

  // Notes on the sheet:
  //   way that makes much much more sense is to connect the selector (three state) to the write enable (and each 64K chip's output at the end)
endmodule

module RAM256Kx8_But_IntendedWay (
  input  [17:0] S,
  input  WriteEn,
  input  [7:0] DataIn,
  input  ReadEn,
  input  CS,
  input  CLK,
  output [7:0] out_7
);

  wire and_1_out, and_2_out, and_3_out, and_4_out, decoder_1_out0, decoder_1_out1, decoder_1_out2,
       decoder_1_out3;
  wire [7:0] ram64kx8_1_dataout, ram64kx8_2_dataout, ram64kx8_3_dataout, ram64kx8_4_dataout;

  Decoder #(.select(2)) decoder_1 (
    .out0(decoder_1_out0), .out1(decoder_1_out1), .out2(decoder_1_out2), .out3(decoder_1_out3),
    .sel(S[17:16]), .en(CS));
  and and_1 (and_1_out, WriteEn, decoder_1_out1);
  and and_2 (and_2_out, WriteEn, decoder_1_out2);
  and and_3 (and_3_out, WriteEn, decoder_1_out3);
  and and_4 (and_4_out, WriteEn, decoder_1_out0);
  RAM64Kx8 ram64kx8_1 (
    .S(S[15:0]), .WriteEn(and_4_out), .ReadEn(ReadEn), .DataIn(DataIn), .CLK(CLK),
    .DataOut(ram64kx8_1_dataout));
  RAM64Kx8 ram64kx8_2 (
    .S(S[15:0]), .WriteEn(and_1_out), .ReadEn(ReadEn), .DataIn(DataIn), .CLK(CLK),
    .DataOut(ram64kx8_2_dataout));
  RAM64Kx8 ram64kx8_3 (
    .S(S[15:0]), .WriteEn(and_2_out), .ReadEn(ReadEn), .DataIn(DataIn), .CLK(CLK),
    .DataOut(ram64kx8_3_dataout));
  RAM64Kx8 ram64kx8_4 (
    .S(S[15:0]), .WriteEn(and_3_out), .ReadEn(ReadEn), .DataIn(DataIn), .CLK(CLK),
    .DataOut(ram64kx8_4_dataout));
  assign out_7 = decoder_1_out0 ? ram64kx8_1_dataout : 8'bz;  // Controlled_Buffer controlled_buffer_1
  assign out_7 = decoder_1_out1 ? ram64kx8_2_dataout : 8'bz;  // Controlled_Buffer controlled_buffer_2
  assign out_7 = decoder_1_out2 ? ram64kx8_3_dataout : 8'bz;  // Controlled_Buffer controlled_buffer_3
  assign out_7 = decoder_1_out3 ? ram64kx8_4_dataout : 8'bz;  // Controlled_Buffer controlled_buffer_4
endmodule

module RAM256Kx16 (
  input  [17:0] S,
  input  WE,
  input  RE,
  input  [15:0] DataIn,
  input  CS,
  output [15:0] out_6
);

  wire and_1_out, and_2_out, and_3_out, and_4_out, CLK_out, decoder_1_out0, decoder_1_out1, decoder_1_out2,
       decoder_1_out3;
  wire [7:0] ram64kx8_1_dataout, ram64kx8_2_dataout, ram64kx8_3_dataout, ram64kx8_4_dataout,
       ram64kx8_5_dataout, ram64kx8_6_dataout, ram64kx8_7_dataout, ram64kx8_8_dataout;

  Decoder #(.select(2)) decoder_1 (
    .out0(decoder_1_out0), .out1(decoder_1_out1), .out2(decoder_1_out2), .out3(decoder_1_out3),
    .sel(S[17:16]), .en(CS));
  Clock CLK (.out(CLK_out));
  and and_1 (and_1_out, WE, decoder_1_out1);
  and and_2 (and_2_out, WE, decoder_1_out0);
  and and_3 (and_3_out, WE, decoder_1_out1);
  and and_4 (and_4_out, WE, decoder_1_out3);
  RAM64Kx8 ram64kx8_1 (
    .S(S[15:0]), .WriteEn(and_2_out), .ReadEn(RE), .DataIn(DataIn[7:0]), .CLK(CLK_out),
    .DataOut(ram64kx8_1_dataout));
  RAM64Kx8 ram64kx8_2 (
    .S(S[15:0]), .WriteEn(and_3_out), .ReadEn(RE), .DataIn(DataIn[7:0]), .CLK(CLK_out),
    .DataOut(ram64kx8_2_dataout));
  RAM64Kx8 ram64kx8_3 (
    .S(S[15:0]), .WriteEn(and_1_out), .ReadEn(RE), .DataIn(DataIn[7:0]), .CLK(CLK_out),
    .DataOut(ram64kx8_3_dataout));
  RAM64Kx8 ram64kx8_4 (
    .S(S[15:0]), .WriteEn(and_4_out), .ReadEn(RE), .DataIn(DataIn[7:0]), .CLK(CLK_out),
    .DataOut(ram64kx8_4_dataout));
  RAM64Kx8 ram64kx8_5 (
    .S(S[15:0]), .WriteEn(and_2_out), .ReadEn(RE), .DataIn(DataIn[15:8]), .CLK(CLK_out),
    .DataOut(ram64kx8_5_dataout));
  RAM64Kx8 ram64kx8_6 (
    .S(S[15:0]), .WriteEn(and_3_out), .ReadEn(RE), .DataIn(DataIn[15:8]), .CLK(CLK_out),
    .DataOut(ram64kx8_6_dataout));
  RAM64Kx8 ram64kx8_7 (
    .S(S[15:0]), .WriteEn(and_1_out), .ReadEn(RE), .DataIn(DataIn[15:8]), .CLK(CLK_out),
    .DataOut(ram64kx8_7_dataout));
  RAM64Kx8 ram64kx8_8 (
    .S(S[15:0]), .WriteEn(and_4_out), .ReadEn(RE), .DataIn(DataIn[15:8]), .CLK(CLK_out),
    .DataOut(ram64kx8_8_dataout));
  assign out_6 = decoder_1_out0 ? {ram64kx8_5_dataout, ram64kx8_1_dataout} : 16'bz;  // Controlled_Buffer controlled_buffer_1
  assign out_6 = decoder_1_out1 ? {ram64kx8_6_dataout, ram64kx8_2_dataout} : 16'bz;  // Controlled_Buffer controlled_buffer_2
  assign out_6 = decoder_1_out2 ? {ram64kx8_7_dataout, ram64kx8_3_dataout} : 16'bz;  // Controlled_Buffer controlled_buffer_3
  assign out_6 = decoder_1_out3 ? {ram64kx8_8_dataout, ram64kx8_4_dataout} : 16'bz;  // Controlled_Buffer controlled_buffer_4

  // Notes on the sheet:
  //   wider: bigger data
  //   larger: more memory addresses
  //   i think this isnt working
endmodule
