// Logisim project Sem1PostUTS.circ as structural Verilog: 28 circuits, main circuit SR_Latch_w_NAND
module Main (
  input  D,
  input  C,
  output out_3,
  output out_4,
  output out_5,
  output out_6
);

  wire not_1_out;

  not not_1 (not_1_out, D);
  SR_Master_Slave_FlipFlop sr_master_slave_flipflop_1 (.S(D), .C(C), .R(not_1_out), .Q(out_3), .Qcomp(out_4));
  NegEdge_D_FlipFlop negedge_d_flipflop_1 (.D(D), .C(C), .Q(out_5), .Qcomp(out_6));
endmodule

module SR_Latch_w_NAND (
  input  S,
  input  R,
  output Q,
  output Qcomp
);

  wire not_1_out, not_2_out;

  not not_1 (not_1_out, S);
  not not_2 (not_2_out, R);
  nand nand_1 (Q, not_1_out, Qcomp);
  nand nand_2 (Qcomp, Q, not_2_out);
endmodule

module Clock_SR_Latch_w_NAND (
  input  S,
  input  C,
  input  R,
  output Q,
  output Qcomp
);

  wire nand_1_out, nand_2_out;

  nand nand_1 (nand_1_out, S, C);
  nand nand_2 (nand_2_out, C, R);
  nand nand_3 (Q, nand_1_out, Qcomp);
  nand nand_4 (Qcomp, Q, nand_2_out);
endmodule

module D_Latch (
  input  D,
  input  C,
  output out_3,
  output out_4
);

  wire not_1_out;

  not not_1 (not_1_out, D);
  Clock_SR_Latch_w_NAND clock_sr_latch_w_nand_1 (.S(D), .C(C), .R(not_1_out), .Q(out_3), .Qcomp(out_4));
endmodule

module Latch_Timing_Problem (
  input  C,
  output Y
);

  wire d_latch_1_out_4;

  D_Latch d_latch_1 (.D(d_latch_1_out_4), .C(C), .out_3(Y), .out_4(d_latch_1_out_4));
endmodule

module SR_Master_Slave_FlipFlop (
  input  S,
  input  C,
  input  R,
  output Q,
  output Qcomp
);

  wire clock_sr_latch_w_nand_1_q, clock_sr_latch_w_nand_1_qcomp, not_1_out;

  not not_1 (not_1_out, C);
  Clock_SR_Latch_w_NAND clock_sr_latch_w_nand_1 (
    .S(S), .C(C), .R(R), .Q(clock_sr_latch_w_nand_1_q), .Qcomp(clock_sr_latch_w_nand_1_qcomp));
  Clock_SR_Latch_w_NAND clock_sr_latch_w_nand_2 (
    .S(clock_sr_latch_w_nand_1_q), .C(not_1_out), .R(clock_sr_latch_w_nand_1_qcomp), .Q(Q), .Qcomp(Qcomp));
endmodule

module NegEdge_D_FlipFlop (
  input  D,
  input  C,
  output Q,
  output Qcomp
);

  wire not_1_out;

  not not_1 (not_1_out, D);
  SR_Master_Slave_FlipFlop sr_master_slave_flipflop_1 (.S(D), .C(C), .R(not_1_out), .Q(Q), .Qcomp(Qcomp));
endmodule

module PosEdge_D_FlipFlop (
  input  D,
  input  C,
  output Q,
  output Qcomp
);

  wire not_1_out, not_2_out;

  not not_1 (not_1_out, C);
  not not_2 (not_2_out, D);
  SR_Master_Slave_FlipFlop sr_master_slave_flipflop_1 (.S(D), .C(not_1_out), .R(not_2_out), .Q(Q), .Qcomp(Qcomp));
endmodule

module CircSequential (
  input  X,
  input  C,
  input  Reset,
  output Y1,
  output Z,
  output Y2
);

  wire d_ff_2_qn, nand_1_out, nand_2_out, nand_3_out, nand_4_out;

  nand nand_1 (nand_1_out, Y1, Y2);
  nand nand_2 (nand_2_out, Y2, X);
  nand nand_3 (nand_3_out, nand_1_out, nand_2_out);
  D_Flip_Flop d_ff_1 (.D(nand_3_out), .clk(C), .Q(Y1), .reset(Reset));  // open: Qn, preset
  D_Flip_Flop d_ff_2 (.D(X), .clk(C), .Q(Y2), .Qn(d_ff_2_qn), .reset(Reset));  // open: preset
  nand nand_4 (nand_4_out, Y1, X, d_ff_2_qn);
  nand nand_5 (Z, nand_4_out, nand_4_out);
endmodule

module JKFlipFlop (
  input  J,
  input  C,
  input  K
);

  wire and_1_out, and_2_out, not_1_out, or_1_out, posedge_d_flipflop_1_q, posedge_d_flipflop_1_qcomp;

  not not_1 (not_1_out, K);
  and and_1 (and_1_out, posedge_d_flipflop_1_qcomp, J);
  and and_2 (and_2_out, not_1_out, posedge_d_flipflop_1_q);
  or or_1 (or_1_out, and_1_out, and_2_out);
  PosEdge_D_FlipFlop posedge_d_flipflop_1 (
    .D(or_1_out), .C(C), .Q(posedge_d_flipflop_1_q), .Qcomp(posedge_d_flipflop_1_qcomp));
endmodule

module JKCircuit (
  input  x,
  output A,
  output B
);

  wire and_1_out, and_2_out, C_out, not_1_out, not_2_out, xor_1_out;

  not not_1 (not_1_out, x);
  Clock C (.out(C_out));
  and and_1 (and_1_out, B, not_1_out);
  and and_2 (and_2_out, B, x);
  xor xor_1 (xor_1_out, x, A);
  not not_2 (not_2_out, xor_1_out);
  J_K_Flip_Flop j_k_ff_1 (.J(and_1_out), .K(and_2_out), .clk(C_out), .Q(A));  // open: Qn, preset, reset
  J_K_Flip_Flop j_k_ff_2 (.J(x), .K(not_2_out), .clk(C_out), .Q(B));  // open: Qn, preset, reset
endmodule

module JKCircuit_w_NAND (
  input  x,
  output A,
  output B
);

  wire C_out, nand_1_out, nand_2_out, nand_3_out, nand_4_out, nand_5_out, nand_6_out, nand_7_out, nand_8_out;

  Clock C (.out(C_out));
  nand nand_1 (nand_1_out, x, x);
  nand nand_2 (nand_2_out, B, nand_1_out);
  nand nand_3 (nand_3_out, B, x);
  nand nand_4 (nand_4_out, x, A);
  nand nand_5 (nand_5_out, nand_1_out, nand_6_out);
  nand nand_6 (nand_6_out, A, A);
  nand nand_7 (nand_7_out, nand_2_out, nand_2_out);
  nand nand_8 (nand_8_out, nand_4_out, nand_5_out);
  J_K_Flip_Flop j_k_ff_1 (.J(nand_7_out), .K(nand_3_out), .clk(C_out), .Q(A));  // open: Qn, preset, reset
  J_K_Flip_Flop j_k_ff_2 (.J(x), .K(nand_8_out), .clk(C_out), .Q(B));  // open: Qn, preset, reset
endmodule

module DCircuit (
  input  x,
  output y
);

  // NAND_Gate nand_1 has open pins: in0=x, in1=x, out=open
  Clock C ();  // open: out
  // NAND_Gate nand_2 is placed but not wired
  D_Flip_Flop d_ff_1 ();  // open: D, clk, Q, Qn, preset, reset
  D_Flip_Flop d_ff_2 ();  // open: D, clk, Q, Qn, preset, reset
endmodule

module PIPO (
  input  [3:0] I,
  input  R,
  output [3:0] O
);

  wire C_out;

  Clock C (.out(C_out));
  D_Flip_Flop d_ff_1 (.D(I[3]), .clk(C_out), .Q(O[3]), .reset(R));  // open: Qn, preset
  D_Flip_Flop d_ff_2 (.D(I[2]), .clk(C_out), .Q(O[2]), .reset(R));  // open: Qn, preset
  D_Flip_Flop d_ff_3 (.D(I[1]), .clk(C_out), .Q(O[1]), .reset(R));  // open: Qn, preset
  D_Flip_Flop d_ff_4 (.D(I[0]), .clk(C_out), .Q(O[0]), .reset(R));  // open: Qn, preset
endmodule

module PIPO_1st_Solution (
  input  [3:0] I,
  input  Load,
  input  R,
  output [3:0] O
);

  wire and_1_out, C_out;

  Clock C (.out(C_out));
  D_Flip_Flop d_ff_1 (.D(I[3]), .clk(and_1_out), .Q(O[3]), .reset(R));  // open: Qn, preset
  D_Flip_Flop d_ff_2 (.D(I[2]), .clk(and_1_out), .Q(O[2]), .reset(R));  // open: Qn, preset
  D_Flip_Flop d_ff_3 (.D(I[1]), .clk(and_1_out), .Q(O[1]), .reset(R));  // open: Qn, preset
  D_Flip_Flop d_ff_4 (.D(I[0]), .clk(and_1_out), .Q(O[0]), .reset(R));  // open: Qn, preset
  and and_1 (and_1_out, C_out, Load);
endmodule

module PIPO_2nd_Solution (
  input  [3:0] I,
  input  Load,
  input  R,
  output [3:0] O
);

  wire C_out, multiplexer_1_out, multiplexer_2_out, multiplexer_3_out, multiplexer_4_out;

  Clock C (.out(C_out));
  D_Flip_Flop d_ff_1 (.D(multiplexer_1_out), .clk(C_out), .Q(O[3]), .reset(R));  // open: Qn, preset
  Multiplexer multiplexer_1 (.in0(O[3]), .in1(I[3]), .out(multiplexer_1_out), .sel(Load));
  D_Flip_Flop d_ff_2 (.D(multiplexer_2_out), .clk(C_out), .Q(O[2]), .reset(R));  // open: Qn, preset
  Multiplexer multiplexer_2 (.in0(O[2]), .in1(I[2]), .out(multiplexer_2_out), .sel(Load));
  D_Flip_Flop d_ff_3 (.D(multiplexer_3_out), .clk(C_out), .Q(O[1]), .reset(R));  // open: Qn, preset
  Multiplexer multiplexer_3 (.in0(O[1]), .in1(I[1]), .out(multiplexer_3_out), .sel(Load));
  D_Flip_Flop d_ff_4 (.D(multiplexer_4_out), .clk(C_out), .Q(O[0]), .reset(R));  // open: Qn, preset
  Multiplexer multiplexer_4 (.in0(O[0]), .in1(I[0]), .out(multiplexer_4_out), .sel(Load));

  // Notes on the sheet:
  //   Bolognese
endmodule

module Notation_circuit (
  input  X,
  input  K1,
  output [3:0] R1,
  output [3:0] R2
);

  wire adder_1_cout, adder_2_cout, adder_3_cout;

  Clock C ();  // open: out
  Controlled_Inverter #(.width(4)) controlled_inverter_1 (.in(R2), .en(X));  // open: out
  Adder adder_1 (.cin(X), .cout(adder_1_cout));  // open: a, b, out
  Adder adder_2 (.cin(adder_1_cout), .cout(adder_2_cout));  // open: a, b, out
  Adder adder_3 (.cin(adder_2_cout), .cout(adder_3_cout));  // open: a, b, out
  Adder adder_4 (.cin(adder_3_cout));  // open: a, b, out, cout

  // Notes on the sheet:
  //   X'.K1: R1 <- R1 + R2
  //   X.K1: R1 <- R1 + R2' + 1
endmodule

module Notation_mux (
  input  K1,
  input  K2,
  input  [3:0] in_3,
  input  [3:0] in_4,
  input  in_5,
  output [3:0] out_6
);

  wire clock_1_out, or_1_out;
  wire [3:0] multiplexer_1_out, R1_q, R2_q;

  Clock clock_1 (.out(clock_1_out));
  Register #(.width(4)) R1 (.D(in_3), .en(in_5), .clk(clock_1_out), .Q(R1_q));  // open: clr
  Register #(.width(4)) R2 (.D(in_4), .en(in_5), .clk(clock_1_out), .Q(R2_q));  // open: clr
  Multiplexer #(.width(4)) multiplexer_1 (.in0(R1_q), .in1(R2_q), .out(multiplexer_1_out), .sel(K1));
  or or_1 (or_1_out, K1, K2);
  Register #(.width(4)) R0 (.D(multiplexer_1_out), .en(or_1_out), .clk(clock_1_out), .Q(out_6));  // open: clr

  // Notes on the sheet:
  //   K1: R0 <- R1
  //   K2.K1': R0<-R2
  //   salah dikit
endmodule

module SISO_SR (
  input  I,
  output O
);

  wire C_out, d_ff_1_q, d_ff_2_q, d_ff_3_q;

  Clock C (.out(C_out));
  D_Flip_Flop d_ff_1 (.D(I), .clk(C_out), .Q(d_ff_1_q));  // open: Qn, preset, reset
  D_Flip_Flop d_ff_2 (.D(d_ff_1_q), .clk(C_out), .Q(d_ff_2_q));  // open: Qn, preset, reset
  D_Flip_Flop d_ff_3 (.D(d_ff_2_q), .clk(C_out), .Q(d_ff_3_q));  // open: Qn, preset, reset
  D_Flip_Flop d_ff_4 (.D(d_ff_3_q), .clk(C_out), .Q(O));  // open: Qn, preset, reset
endmodule

module SISO_SL (
  input  I,
  output O
);

  wire C_out, d_ff_2_q, d_ff_3_q, d_ff_4_q;

  Clock C (.out(C_out));
  D_Flip_Flop d_ff_1 (.D(d_ff_2_q), .clk(C_out), .Q(O));  // open: Qn, preset, reset
  D_Flip_Flop d_ff_2 (.D(d_ff_3_q), .clk(C_out), .Q(d_ff_2_q));  // open: Qn, preset, reset
  D_Flip_Flop d_ff_3 (.D(d_ff_4_q), .clk(C_out), .Q(d_ff_3_q));  // open: Qn, preset, reset
  D_Flip_Flop d_ff_4 (.D(I), .clk(C_out), .Q(d_ff_4_q));  // open: Qn, preset, reset
endmodule

module Ripple_Counter (
  input  Reset
);

  wire C_out, d_ff_1_qn, d_ff_2_qn, d_ff_3_qn, d_ff_4_qn;
  wire [3:0] d_ff_1_q;

  Clock C (.out(C_out));
  D_Flip_Flop d_ff_1 (.D(d_ff_1_qn), .clk(C_out), .Q(d_ff_1_q[0]), .Qn(d_ff_1_qn), .reset(Reset));  // open: preset
  D_Flip_Flop d_ff_2 (.D(d_ff_2_qn), .clk(d_ff_1_qn), .Q(d_ff_1_q[1]), .Qn(d_ff_2_qn), .reset(Reset));  // open: preset
  D_Flip_Flop d_ff_3 (.D(d_ff_3_qn), .clk(d_ff_2_qn), .Q(d_ff_1_q[2]), .Qn(d_ff_3_qn), .reset(Reset));  // open: preset
  D_Flip_Flop d_ff_4 (.D(d_ff_4_qn), .clk(d_ff_3_qn), .Q(d_ff_1_q[3]), .Qn(d_ff_4_qn), .reset(Reset));  // open: preset
  Hex_Digit_Display hex_digit_display_1 (.value(d_ff_1_q));  // open: dp

  // Notes on the sheet:
  //   black magic
endmodule

module Sync_Counter_4bit (
  input  CountE,
  input  R,
  output Q0,
  output Q1,
  output Q2,
  output Q3,
  output En_Out
);

  wire and_1_out, and_2_out, and_3_out, CLK_out, xor_1_out, xor_2_out, xor_3_out, xor_4_out;

  and and_1 (and_1_out, CountE, Q0);
  and and_2 (and_2_out, and_1_out, Q1);
  Clock CLK (.out(CLK_out));
  and and_3 (and_3_out, and_2_out, Q2);
  and and_4 (En_Out, and_3_out, Q3);
  D_Flip_Flop d_ff_1 (.D(xor_1_out), .clk(CLK_out), .Q(Q0), .reset(R));  // open: Qn, preset
  xor xor_1 (xor_1_out, Q0, CountE);
  D_Flip_Flop d_ff_2 (.D(xor_2_out), .clk(CLK_out), .Q(Q1), .preset(R), .reset(R));  // open: Qn
  xor xor_2 (xor_2_out, Q1, and_1_out);
  D_Flip_Flop d_ff_3 (.D(xor_3_out), .clk(CLK_out), .Q(Q2), .preset(R), .reset(R));  // open: Qn
  xor xor_3 (xor_3_out, Q2, and_2_out);
  D_Flip_Flop d_ff_4 (.D(xor_4_out), .clk(CLK_out), .Q(Q3), .preset(R), .reset(R));  // open: Qn
  xor xor_4 (xor_4_out, Q3, and_3_out);
endmodule

module Incrementer_4bit (
  input  CounterE,
  input  I0,
  input  I1,
  input  I2,
  input  I3,
  output O0,
  output O1,
  output O2,
  output O3
);

  wire and_1_out, and_2_out, and_3_out, and_4_out;

  and and_1 (and_1_out, CounterE, I0);
  and and_2 (and_2_out, and_1_out, I1);
  and and_3 (and_3_out, and_2_out, I2);
  and and_4 (and_4_out, and_3_out, I3);
  xor xor_1 (O0, I0, CounterE);
  xor xor_2 (O1, I1, and_1_out);
  xor xor_3 (O2, I2, and_2_out);
  xor xor_4 (O3, I3, and_3_out);
endmodule

module Sync_Counter_8bit (
  input  CountE
);

  wire sync_counter_4bit_1_en_out;

  Sync_Counter_4bit sync_counter_4bit_1 (
    .CountE(CountE), .En_Out(sync_counter_4bit_1_en_out));  // open: R, Q0, Q1, Q2, Q3
  Sync_Counter_4bit sync_counter_4bit_2 (.CountE(sync_counter_4bit_1_en_out));  // open: R, Q0, Q1, Q2, Q3, En_Out
endmodule

module CircuitDesign (
  input  Cx,
  input  Cy
);

  wire A_q, and_1_out, B_q;

  and and_1 (and_1_out, B_q, Cx);
  // XOR_Gate xor_1 has open pins: in0=A_q, out=open
  D_Flip_Flop B (.Q(B_q));  // open: D, clk, Qn, preset, reset
  D_Flip_Flop A (.D(and_1_out), .Q(A_q));  // open: clk, Qn, preset, reset
endmodule

module CombinationalSoalUAS (
  input  X,
  input  Y,
  input  A,
  input  B,
  output DA,
  output DB,
  output Z
);

  wire and_1_out, and_2_out, and_3_out, and_4_out, not_1_out, not_2_out;

  not not_1 (not_1_out, X);
  not not_2 (not_2_out, Y);
  and and_1 (and_1_out, X, A);
  and and_2 (and_2_out, not_1_out, not_2_out);
  and and_3 (and_3_out, X, B);
  and and_4 (and_4_out, not_1_out, A);
  or or_1 (DA, and_1_out, and_2_out);
  or or_2 (DB, and_3_out, and_4_out);
  and and_5 (Z, not_1_out, B);
endmodule

module SequentialSoalUAS (
  input  X,
  input  Y,
  input  R,
  output Z
);

  wire CLK_out, combinationalsoaluas_1_da, combinationalsoaluas_1_db, d_ff_1_q, d_ff_2_q;

  Clock CLK (.out(CLK_out));
  CombinationalSoalUAS combinationalsoaluas_1 (
    .X(X), .Y(Y), .A(d_ff_2_q), .B(d_ff_1_q), .DA(combinationalsoaluas_1_da), .DB(combinationalsoaluas_1_db),
    .Z(Z));
  D_Flip_Flop d_ff_1 (.D(combinationalsoaluas_1_da), .clk(CLK_out), .Q(d_ff_1_q), .reset(R));  // open: Qn, preset
  D_Flip_Flop d_ff_2 (.D(combinationalsoaluas_1_db), .clk(CLK_out), .Q(d_ff_2_q), .reset(R));  // open: Qn, preset
endmodule

module Combinational2 (
  input  A,
  input  B,
  input  Y,
  output DA,
  output DB,
  output Z
);

  wire and_1_out, and_2_out, and_3_out, not_1_out, not_2_out, not_3_out, xor_1_out;

  not not_1 (not_1_out, A);
  not not_2 (not_2_out, B);
  not not_3 (not_3_out, Y);
  and and_1 (and_1_out, B, Y);
  and and_2 (and_2_out, not_1_out, B);
  and and_3 (and_3_out, A, not_2_out, not_3_out);
  or or_1 (DA, and_1_out, and_2_out, and_3_out);
  and and_4 (DB, not_1_out, Y);
  xor xor_1 (xor_1_out, A, B);
  not not_4 (Z, xor_1_out);
endmodule
