// Logisim project Sem1PostUTSPart2.circ as structural Verilog: 13 circuits, main circuit RegisterCirc_w_Decoder
module RegisterCirc_w_Decoder (
  input  B3,
  input  B2,
  input  B1,
  input  B0,
  input  Cx,
  input  Cy,
  output A3,
  output A2,
  output A1,
  output A0
);

  wire and_1_out, and_2_out, and_3_out, and_4_out, and_5_out, and_6_out, and_7_out, and_8_out, and_9_out,
       and_10_out, and_11_out, and_12_out, C_out, d_ff_1_q, d_ff_2_q, d_ff_3_q, d_ff_4_q, decoder_1_out0,
       decoder_1_out1, decoder_1_out2, or_1_out, or_2_out, or_3_out, or_4_out, or_5_out, or_6_out, or_7_out,
       or_8_out, xor_1_out, xor_2_out, xor_3_out, xor_4_out;

  D_Flip_Flop d_ff_1 (.D(B3), .clk(C_out), .Q(d_ff_1_q));  // open: Qn, preset, reset
  D_Flip_Flop d_ff_2 (.D(B2), .clk(C_out), .Q(d_ff_2_q));  // open: Qn, preset, reset
  D_Flip_Flop d_ff_3 (.D(B1), .clk(C_out), .Q(d_ff_3_q));  // open: Qn, preset, reset
  D_Flip_Flop d_ff_4 (.D(B0), .clk(C_out), .Q(d_ff_4_q));  // open: Qn, preset, reset
  Clock C (.out(C_out));
  Decoder #(.select(2)) decoder_1 (
    .out0(decoder_1_out0), .out1(decoder_1_out1), .out2(decoder_1_out2), .sel({Cy, Cx}));  // open: out3, en
  xor xor_1 (xor_1_out, A3, d_ff_1_q);
  or or_1 (or_1_out, A3, d_ff_1_q);
  xor xor_2 (xor_2_out, A2, d_ff_2_q);
  or or_2 (or_2_out, A2, d_ff_2_q);
  xor xor_3 (xor_3_out, A1, d_ff_3_q);
  or or_3 (or_3_out, A1, d_ff_3_q);
  xor xor_4 (xor_4_out, A0, d_ff_4_q);
  or or_4 (or_4_out, A0, d_ff_4_q);
  and and_1 (and_1_out, A3, decoder_1_out0);
  and and_2 (and_2_out, xor_1_out, decoder_1_out1);
  and and_3 (and_3_out, or_1_out, decoder_1_out2);
  and and_4 (and_4_out, A2, decoder_1_out0);
  and and_5 (and_5_out, xor_2_out, decoder_1_out1);
  and and_6 (and_6_out, or_2_out, decoder_1_out2);
  and and_7 (and_7_out, A1, decoder_1_out0);
  and and_8 (and_8_out, xor_3_out, decoder_1_out1);
  and and_9 (and_9_out, or_3_out, decoder_1_out2);
  and and_10 (and_10_out, A0, decoder_1_out0);
  and and_11 (and_11_out, xor_4_out, decoder_1_out1);
  and and_12 (and_12_out, or_4_out, decoder_1_out2);
  or or_5 (or_5_out, and_1_out, and_2_out, and_3_out);
  or or_6 (or_6_out, and_4_out, and_5_out, and_6_out);
  or or_7 (or_7_out, and_7_out, and_8_out, and_9_out);
  or or_8 (or_8_out, and_10_out, and_11_out, and_12_out);
  D_Flip_Flop d_ff_5 (.D(or_5_out), .clk(C_out), .Q(A3));  // open: Qn, preset, reset
  D_Flip_Flop d_ff_6 (.D(or_6_out), .clk(C_out), .Q(A2));  // open: Qn, preset, reset
  D_Flip_Flop d_ff_7 (.D(or_7_out), .clk(C_out), .Q(A1));  // open: Qn, preset, reset
  D_Flip_Flop d_ff_8 (.D(or_8_out), .clk(C_out), .Q(A0));  // open: Qn, preset, reset

  // Notes on the sheet:
  //   Design procedure selalu lebioh kecil gate costnya
endmodule

module MuxBasedTransfer_3R (
  input  S0,
  input  L0,
  input  S1,
  input  L1,
  input  S2,
  input  L2
);

  wire clock_1_out;
  wire [3:0] multiplexer_1_out, multiplexer_2_out, multiplexer_3_out, R0_q, R1_q, R2_q;

  Multiplexer #(.width(4)) multiplexer_1 (.in0(R1_q), .in1(R0_q), .out(multiplexer_1_out), .sel(S0));
  Multiplexer #(.width(4)) multiplexer_2 (.in0(R2_q), .in1(R0_q), .out(multiplexer_2_out), .sel(S1));
  Multiplexer #(.width(4)) multiplexer_3 (.in0(R2_q), .in1(R1_q), .out(multiplexer_3_out), .sel(S2));
  Clock clock_1 (.out(clock_1_out));
  Register #(.width(4)) R0 (.D(multiplexer_1_out), .en(L0), .clk(clock_1_out), .Q(R0_q));  // open: clr
  Register #(.width(4)) R1 (.D(multiplexer_2_out), .en(L1), .clk(clock_1_out), .Q(R1_q));  // open: clr
  Register #(.width(4)) R2 (.D(multiplexer_3_out), .en(L2), .clk(clock_1_out), .Q(R2_q));  // open: clr
endmodule

module MuxBasedTransfer_4R (
  input  [3:0] D0,
  input  L0,
  input  [1:0] S0,
  input  [3:0] D1,
  input  L1,
  input  [1:0] S1,
  input  [3:0] D2,
  input  L2,
  input  [1:0] S2,
  input  [3:0] D3,
  input  L3,
  input  [1:0] S3
);

  wire clock_1_out;
  wire [3:0] multiplexer_1_out, multiplexer_2_out, multiplexer_3_out, multiplexer_4_out, R0_q, R1_q, R2_q,
       register_1_q;

  Multiplexer #(.select(2), .width(4)) multiplexer_1 (
    .in0(D0), .in1(R1_q), .in2(R2_q), .in3(register_1_q), .out(multiplexer_1_out), .sel(S0));
  Multiplexer #(.select(2), .width(4)) multiplexer_2 (
    .in0(D1), .in1(R0_q), .in2(R2_q), .in3(register_1_q), .out(multiplexer_2_out), .sel(S1));
  Multiplexer #(.select(2), .width(4)) multiplexer_3 (
    .in0(D2), .in1(R0_q), .in2(R1_q), .in3(register_1_q), .out(multiplexer_3_out), .sel(S2));
  Multiplexer #(.select(2), .width(4)) multiplexer_4 (
    .in0(D3), .in1(R0_q), .in2(R1_q), .in3(R2_q), .out(multiplexer_4_out), .sel(S3));
  Clock clock_1 (.out(clock_1_out));
  Register #(.width(4)) R0 (.D(multiplexer_1_out), .en(L0), .clk(clock_1_out), .Q(R0_q));  // open: clr
  Register #(.width(4)) R1 (.D(multiplexer_2_out), .en(L1), .clk(clock_1_out), .Q(R1_q));  // open: clr
  Register #(.width(4)) R2 (.D(multiplexer_3_out), .en(L2), .clk(clock_1_out), .Q(R2_q));  // open: clr
  Register #(.width(4)) register_1 (.D(multiplexer_4_out), .en(L3), .clk(clock_1_out), .Q(register_1_q));  // open: clr
  Hex_Digit_Display hex_digit_display_1 (.value(R0_q));  // open: dp
  Hex_Digit_Display hex_digit_display_2 (.value(R1_q));  // open: dp
  Hex_Digit_Display hex_digit_display_3 (.value(R2_q));  // open: dp
  Hex_Digit_Display hex_digit_display_4 (.value(register_1_q));  // open: dp
endmodule

module BusMuxBasedTransfer_3R (
  input  L0,
  input  [3:0] D,
  input  [1:0] S,
  input  L1,
  input  L2
);

  wire [3:0] multiplexer_1_out, R0_q, R1_q, R2_q;

  Multiplexer #(.select(2), .width(4)) multiplexer_1 (
    .in0(D), .in1(R0_q), .in2(R1_q), .in3(R2_q), .out(multiplexer_1_out), .sel(S));
  Register #(.width(4)) R0 (.D(multiplexer_1_out), .en(L0), .Q(R0_q));  // open: clk, clr
  Register #(.width(4)) R1 (.D(multiplexer_1_out), .en(L1), .Q(R1_q));  // open: clk, clr
  Register #(.width(4)) R2 (.D(multiplexer_1_out), .en(L2), .Q(R2_q));  // open: clk, clr
endmodule

module SelfRegister (
  input  [3:0] D,
  input  WE,
  input  C,
  output [3:0] Q,
  output [3:0] Qnot
);

  wire and_1_out;

  and and_1 (and_1_out, WE, C);
  D_Flip_Flop d_ff_1 (.D(D[0]), .clk(and_1_out), .Q(Q[0]), .Qn(Qnot[0]));  // open: preset, reset
  D_Flip_Flop d_ff_2 (.D(D[1]), .clk(and_1_out), .Q(Q[1]), .Qn(Qnot[1]));  // open: preset, reset
  D_Flip_Flop d_ff_3 (.D(D[2]), .clk(and_1_out), .Q(Q[2]), .Qn(Qnot[2]));  // open: preset, reset
  D_Flip_Flop d_ff_4 (.D(D[3]), .clk(and_1_out), .Q(Q[3]), .Qn(Qnot[3]));  // open: preset, reset
endmodule

module BusThreeStateTransfer_3R (
  input  [3:0] D,
  input  L0,
  input  [1:0] S,
  input  L1,
  input  L2
);

  wire [3:0] R0_q, R1_q, R2_q, threestatemux_4to1_4bit_1_o;

  ThreeStateMux_4to1_4bit threestatemux_4to1_4bit_1 (
    .I0(D), .I1(R0_q), .I2(R1_q), .I3(R2_q), .S(S), .O(threestatemux_4to1_4bit_1_o));
  Register #(.width(4)) R0 (.D(threestatemux_4to1_4bit_1_o), .en(L0), .Q(R0_q));  // open: clk, clr
  Register #(.width(4)) R1 (.D(threestatemux_4to1_4bit_1_o), .en(L1), .Q(R1_q));  // open: clk, clr
  Register #(.width(4)) R2 (.D(threestatemux_4to1_4bit_1_o), .en(L2), .Q(R2_q));  // open: clk, clr
endmodule

module ThreeStateMux_4to1_4bit (
  input  [3:0] I0,
  input  [3:0] I1,
  input  [3:0] I2,
  input  [3:0] I3,
  input  [1:0] S,
  output [3:0] O
);

  wire not_1_out, not_2_out;
  wire [3:0] controlled_buffer_1_out, controlled_buffer_3_out;

  not not_1 (not_1_out, S[0]);
  assign controlled_buffer_1_out = not_1_out ? I0 : 4'bz;  // Controlled_Buffer controlled_buffer_1
  assign controlled_buffer_1_out = S[0] ? I1 : 4'bz;  // Controlled_Buffer controlled_buffer_2
  assign controlled_buffer_3_out = not_1_out ? I2 : 4'bz;  // Controlled_Buffer controlled_buffer_3
  assign controlled_buffer_3_out = S[0] ? I3 : 4'bz;  // Controlled_Buffer controlled_buffer_4
  not not_2 (not_2_out, S[1]);
  assign O = not_2_out ? controlled_buffer_1_out : 4'bz;  // Controlled_Buffer controlled_buffer_5
  assign O = S[1] ? controlled_buffer_3_out : 4'bz;  // Controlled_Buffer controlled_buffer_6
endmodule

module ThreeStateMux_4to1_1bit (
  input  I0,
  input  I1,
  input  I2,
  input  I3,
  input  [1:0] S,
  output O
);

  wire controlled_buffer_1_out, controlled_buffer_3_out, not_1_out, not_2_out;

  not not_1 (not_1_out, S[0]);
  assign controlled_buffer_1_out = not_1_out ? I0 : 1'bz;  // Controlled_Buffer controlled_buffer_1
  assign controlled_buffer_1_out = S[0] ? I1 : 1'bz;  // Controlled_Buffer controlled_buffer_2
  assign controlled_buffer_3_out = not_1_out ? I2 : 1'bz;  // Controlled_Buffer controlled_buffer_3
  assign controlled_buffer_3_out = S[0] ? I3 : 1'bz;  // Controlled_Buffer controlled_buffer_4
  not not_2 (not_2_out, S[1]);
  assign O = not_2_out ? controlled_buffer_1_out : 1'bz;  // Controlled_Buffer controlled_buffer_5
  assign O = S[1] ? controlled_buffer_3_out : 1'bz;  // Controlled_Buffer controlled_buffer_6
endmodule

module BusThreeStateTransfer_fixed (
  input  [3:0] D,
  input  L0,
  input  L1,
  input  L2,
  input  [1:0] S
);

  wire C_out;
  wire [3:0] R0_q, R1_q, R2_q, threestatemux_4to1_1bit_1_o;

  Clock C (.out(C_out));
  ThreeStateMux_4to1_1bit threestatemux_4to1_1bit_1 (
    .I0(D[0]), .I1(R0_q[0]), .I2(R1_q[0]), .I3(R2_q[0]), .S(S), .O(threestatemux_4to1_1bit_1_o[0]));
  ThreeStateMux_4to1_1bit threestatemux_4to1_1bit_2 (
    .I0(D[1]), .I1(R0_q[1]), .I2(R1_q[1]), .I3(R2_q[1]), .S(S), .O(threestatemux_4to1_1bit_1_o[1]));
  ThreeStateMux_4to1_1bit threestatemux_4to1_1bit_3 (
    .I0(D[2]), .I1(R0_q[2]), .I2(R1_q[2]), .I3(R2_q[2]), .S(S), .O(threestatemux_4to1_1bit_1_o[2]));
  ThreeStateMux_4to1_1bit threestatemux_4to1_1bit_4 (
    .I0(D[3]), .I1(R0_q[3]), .I2(R1_q[3]), .I3(R2_q[3]), .S(S), .O(threestatemux_4to1_1bit_1_o[3]));
  Register #(.width(4)) R0 (.D(threestatemux_4to1_1bit_1_o), .en(L0), .clk(C_out), .Q(R0_q));  // open: clr
  Register #(.width(4)) R1 (.D(threestatemux_4to1_1bit_1_o), .en(L1), .clk(C_out), .Q(R1_q));  // open: clr
  Register #(.width(4)) R2 (.D(threestatemux_4to1_1bit_1_o), .en(L2), .clk(C_out), .Q(R2_q));  // open: clr
endmodule

module SRG_4_2x (
  input  [3:0] I2,
  input  [3:0] I1,
  input  Load,
  output O
);

  wire CLK_out, srg_4_1_o;

  Clock CLK (.out(CLK_out));
  SRG_4 srg_4_1 (.I(I1), .Cin(O), .Load(Load), .CLK(CLK_out), .O(srg_4_1_o));
  SRG_4 srg_4_2 (.I(I2), .Cin(srg_4_1_o), .Load(Load), .CLK(CLK_out), .O(O));
endmodule

module SRG_4 (
  input  [3:0] I,
  input  Cin,
  input  Load,
  input  CLK,
  output O
);

  wire d_ff_1_q, d_ff_2_q, d_ff_3_q, multiplexer_1_out, multiplexer_2_out, multiplexer_3_out,
       multiplexer_4_out, not_1_out;

  not not_1 (not_1_out, Load);
  D_Flip_Flop d_ff_1 (.D(multiplexer_1_out), .clk(CLK), .Q(d_ff_1_q));  // open: Qn, preset, reset
  Multiplexer multiplexer_1 (.in0(I[3]), .in1(Cin), .out(multiplexer_1_out), .sel(not_1_out));
  D_Flip_Flop d_ff_2 (.D(multiplexer_2_out), .clk(CLK), .Q(d_ff_2_q));  // open: Qn, preset, reset
  Multiplexer multiplexer_2 (.in0(I[2]), .in1(d_ff_1_q), .out(multiplexer_2_out), .sel(not_1_out));
  // Shift_Register #(.length(4)) shift_register_1: pin names not known
  D_Flip_Flop d_ff_3 (.D(multiplexer_3_out), .clk(CLK), .Q(d_ff_3_q));  // open: Qn, preset, reset
  Multiplexer multiplexer_3 (.in0(I[1]), .in1(d_ff_2_q), .out(multiplexer_3_out), .sel(not_1_out));
  D_Flip_Flop d_ff_4 (.D(multiplexer_4_out), .clk(CLK), .Q(O));  // open: Qn, preset, reset
  Multiplexer multiplexer_4 (.in0(I[0]), .in1(d_ff_3_q), .out(multiplexer_4_out), .sel(not_1_out));
endmodule

module Serial_Adder_Parallel_In (
  input  [3:0] Ain,
  input  [3:0] Bin,
  input  Load
);

  wire A_o, adder_1_cout, adder_1_out, B_o, CLK_out, d_ff_1_q;

  Clock CLK (.out(CLK_out));
  SRG_4 A (.I(Ain), .Cin(adder_1_out), .Load(Load), .CLK(CLK_out), .O(A_o));
  SRG_4 B (.I(Bin), .Load(Load), .CLK(CLK_out), .O(B_o));  // open: Cin
  Adder #(.width(1)) adder_1 (.a(A_o), .b(B_o), .out(adder_1_out), .cin(d_ff_1_q), .cout(adder_1_cout));
  D_Flip_Flop d_ff_1 (.D(adder_1_cout), .clk(CLK_out), .Q(d_ff_1_q), .reset(Load));  // open: Qn, preset
  LED led_1 (.in(adder_1_out));
endmodule

module Serial_Adder_Serial_In (
  input  Ain,
  input  Bin,
  input  Load
);

  wire A_o, adder_1_cout, adder_1_out, B_o, CLK_out, d_ff_1_q;

  Clock CLK (.out(CLK_out));
  SRG_4 A (.Cin(Ain), .Load(Load), .CLK(CLK_out), .O(A_o));  // open: I
  SRG_4 B (.Cin(Bin), .Load(Load), .CLK(CLK_out), .O(B_o));  // open: I
  Adder #(.width(1)) adder_1 (.a(A_o), .b(B_o), .out(adder_1_out), .cin(d_ff_1_q), .cout(adder_1_cout));
  D_Flip_Flop d_ff_1 (.D(adder_1_cout), .clk(CLK_out), .Q(d_ff_1_q), .reset(Load));  // open: Qn, preset
  LED led_1 (.in(adder_1_out));
endmodule
