// Logisim project 99144.circ as structural Verilog: 2 circuits, main circuit main
module main (
  input  S7,
  input  S6,
  input  S5,
  input  S4,
  input  S3,
  input  S2,
  input  S1,
  input  S0,
  input  A,
  input  B,
  input  Mode
);

  wire [3:0] liftcontroller_1_lift_a, liftcontroller_1_lift_b;

  LiftController liftcontroller_1 (
    .S7(S7), .S6(S6), .S5(S5), .S4(S4), .S3(S3), .S2(S2), .S1(S1), .S0(S0), .A(A), .B(B), .Mode(Mode),
    .Lift_A(liftcontroller_1_lift_a), .Lift_B(liftcontroller_1_lift_b));
  Hex_Digit_Display #(.decimalPoint("false")) Lift_A (.value(liftcontroller_1_lift_a));
  Hex_Digit_Display #(.decimalPoint("false")) Lift_B (.value(liftcontroller_1_lift_b));
endmodule

module LiftController (
  input  S7,
  input  S6,
  input  S5,
  input  S4,
  input  S3,
  input  S2,
  input  S1,
  input  S0,
  input  A,
  input  B,
  input  Mode,
  output [3:0] Lift_A,
  output [3:0] Lift_B
);

  wire and_1_out, and_2_out, and_3_out, and_4_out, and_5_out, not_1_out;
  wire [2:0] priority_encoder_1_out, priority_encoder_2_out;

  not not_1 (not_1_out, Mode);
  and and_1 (and_1_out, not_1_out, S7);
  and and_2 (and_2_out, not_1_out, S5);
  and and_3 (and_3_out, not_1_out, S3);
  and and_4 (and_4_out, not_1_out, S1);
  Priority_Encoder priority_encoder_1 (
    .in0(S0), .in1(and_4_out), .in2(S2), .in3(and_3_out), .in4(S4), .in5(and_2_out), .in6(S6),
    .in7(and_1_out), .out(priority_encoder_1_out));  // open: en_in, gs, en_out
  Priority_Encoder priority_encoder_2 (
    .in1(S1), .in3(S3), .in5(S5), .in7(S7), .out(priority_encoder_2_out));  // open: in0, in2, in4, in6, en_in, gs, en_out
  assign Lift_A = A ? {1'b0, priority_encoder_1_out} : 4'bz;  // Controlled_Buffer controlled_buffer_1
  assign Lift_B = and_5_out ? {1'b0, priority_encoder_2_out} : 4'bz;  // Controlled_Buffer controlled_buffer_2
  and and_5 (and_5_out, B, Mode);

  // Notes on the sheet:
  //   template_A
endmodule
