// Logisim project LAB1_FEIN_2506599144_JovanFinesta.circ as structural Verilog: 3 circuits, main circuit XNORGate
module XNORGate (
  input  IN1,
  input  IN2,
  output OUT1
);

  wire and_1_out, and_2_out, and_3_out, not_1_out, not_2_out, not_3_out, not_4_out;

  not not_1 (not_1_out, IN1);
  not not_2 (not_2_out, IN2);
  and and_1 (and_1_out, IN1, IN2);
  and and_2 (and_2_out, not_1_out, not_2_out);
  not not_3 (not_3_out, and_1_out);
  and and_3 (and_3_out, not_3_out, not_4_out);
  not not_4 (not_4_out, and_2_out);
  not not_5 (OUT1, and_3_out);
endmodule

module Circuit (
  input  A,
  input  B,
  input  C,
  output X,
  output Y
);

  wire and_2_out, and_3_out, not_1_out, not_2_out, xnorgate_1_out1, xnorgate_2_out1;

  XNORGate xnorgate_1 (.IN1(A), .IN2(C), .OUT1(xnorgate_1_out1));
  XNORGate xnorgate_2 (.IN1(A), .IN2(B), .OUT1(xnorgate_2_out1));
  and and_1 (X, A, B, xnorgate_1_out1);
  and and_2 (and_2_out, C, xnorgate_2_out1);
  not not_1 (not_1_out, A);
  not not_2 (not_2_out, and_2_out);
  and and_3 (and_3_out, not_1_out, not_2_out);
  not not_3 (Y, and_3_out);
endmodule

module ORGate (
  input  IN1,
  input  IN2,
  output OUT1
);

  wire and_1_out, not_1_out, not_2_out;

  not not_1 (not_1_out, IN1);
  not not_2 (not_2_out, IN2);
  and and_1 (and_1_out, not_1_out, not_2_out);
  not not_3 (OUT1, and_1_out);
endmodule
