// Logisim project LAB2_FEIN_2506599144_JovanFinesta.circ as structural Verilog: 2 circuits, main circuit SOP
module POS (
  input  A,
  input  B,
  input  C,
  input  D,
  output O
);

  wire not_1_out, not_2_out, not_3_out, not_4_out, not_5_out, not_6_out, not_7_out, not_8_out, not_9_out,
       or_1_out, or_2_out, or_3_out, or_4_out, or_5_out;

  or or_1 (or_1_out, C, D);
  not not_1 (not_1_out, B);
  not not_2 (not_2_out, D);
  or or_2 (or_2_out, not_1_out, C, not_2_out);
  not not_3 (not_3_out, A);
  not not_4 (not_4_out, B);
  not not_5 (not_5_out, C);
  or or_3 (or_3_out, not_3_out, not_4_out, not_5_out);
  not not_6 (not_6_out, B);
  not not_7 (not_7_out, C);
  or or_4 (or_4_out, not_6_out, not_7_out, D);
  not not_8 (not_8_out, A);
  not not_9 (not_9_out, C);
  or or_5 (or_5_out, not_8_out, not_9_out, D);
  and and_1 (O, or_1_out, or_2_out, or_3_out, or_4_out, or_5_out);

  // Notes on the sheet:
  //   POS = (C + D)(B'+C+D')(A'+B'+C')(B'+C'+D)(A'+C'+D) (SALAH)
endmodule

module SOP (
  input  A,
  input  B,
  input  C,
  input  D,
  output O
);

  wire and_1_out, and_2_out, and_3_out, and_4_out, not_1_out, not_2_out, not_3_out, not_4_out, not_5_out;

  not not_1 (not_1_out, A);
  not not_2 (not_2_out, B);
  and and_1 (and_1_out, not_1_out, not_2_out, C);
  not not_3 (not_3_out, A);
  and and_2 (and_2_out, not_3_out, C, D);
  not not_4 (not_4_out, C);
  and and_3 (and_3_out, B, not_4_out, D);
  not not_5 (not_5_out, B);
  and and_4 (and_4_out, not_5_out, C, D);
  or or_1 (O, and_1_out, and_2_out, and_3_out, and_4_out);

  // Notes on the sheet:
  //   SOP = A'B'C + A'CD + BC'D + B'CD
endmodule
