// Logisim project LAB3_FEIN_2506599144_JovanFinesta.circ as structural Verilog: 5 circuits, main circuit DuoBinEnc
module DuoBinEnc (
  input  D0,
  input  D1,
  input  D2,
  input  D3,
  input  D4,
  input  D5,
  input  D6,
  input  D7,
  input  D8,
  input  D9,
  input  DA,
  input  DB,
  output B3,
  output B2,
  output B1,
  output B0
);

  ORGate orgate_1 (.A(D8), .B(D9), .C(DA), .D(DB), .O(B3));  // open: E, F
  ORGate orgate_2 (.A(D4), .B(D5), .C(D6), .D(D7), .O(B2));  // open: E, F
  ORGate orgate_3 (.A(D2), .B(D3), .C(D6), .D(D7), .E(DA), .F(DB), .O(B1));
  ORGate orgate_4 (.A(D1), .B(D3), .C(D5), .D(D7), .E(D9), .F(DB), .O(B0));
endmodule

module DEMUX1_to_8 (
  input  I,
  input  S2,
  input  S1,
  input  S0,
  output Y0,
  output Y1,
  output Y2,
  output Y3,
  output Y4,
  output Y5,
  output Y6,
  output Y7
);

  wire not_1_out, not_2_out, not_3_out, not_4_out, not_5_out, not_6_out, not_7_out, not_8_out, not_9_out,
       not_10_out, not_11_out, not_12_out;

  not not_1 (not_1_out, S2);
  not not_2 (not_2_out, S1);
  not not_3 (not_3_out, S0);
  not not_4 (not_4_out, S2);
  not not_5 (not_5_out, S1);
  not not_6 (not_6_out, S2);
  not not_7 (not_7_out, S0);
  not not_8 (not_8_out, S2);
  not not_9 (not_9_out, S1);
  not not_10 (not_10_out, S0);
  not not_11 (not_11_out, S1);
  not not_12 (not_12_out, S0);
  ANDGate andgate_1 (.A(not_1_out), .B(not_2_out), .C(not_3_out), .D(I), .O(Y0));
  ANDGate andgate_2 (.A(not_4_out), .B(not_5_out), .C(S0), .D(I), .O(Y1));
  ANDGate andgate_3 (.A(not_6_out), .B(S1), .C(not_7_out), .D(I), .O(Y2));
  ANDGate andgate_4 (.A(not_8_out), .B(S1), .C(S0), .D(I), .O(Y3));
  ANDGate andgate_5 (.A(S2), .B(not_9_out), .C(not_10_out), .D(I), .O(Y4));
  ANDGate andgate_6 (.A(S2), .B(not_11_out), .C(S0), .D(I), .O(Y5));
  ANDGate andgate_7 (.A(S2), .B(S1), .C(not_12_out), .D(I), .O(Y6));
  ANDGate andgate_8 (.A(S2), .B(S1), .C(S0), .D(I), .O(Y7));
endmodule

module ANDGate (
  input  A,
  input  B,
  input  C,
  input  D,
  output O
);

  and and_1 (O, A, B, C, D);
endmodule

module ORGate (
  input  A,
  input  B,
  input  C,
  input  D,
  input  E,
  input  F,
  output O
);

  or or_1 (O, A, B, C, D, E, F);
endmodule

module BinOctConv (
  input  D0,
  input  D1,
  input  D2,
  input  D3,
  input  D4,
  input  D5,
  input  D6,
  input  D7,
  input  D8,
  input  D9,
  input  DA,
  input  DB,
  output oktal00,
  output oktal01,
  output oktal02,
  output oktal03,
  output oktal04,
  output oktal05,
  output oktal06,
  output oktal07,
  output oktal10,
  output oktal11,
  output oktal12,
  output oktal13
);

  wire duobinenc_1_b0, duobinenc_1_b1, duobinenc_1_b2, duobinenc_1_b3, not_1_out, not_2_out, not_3_out,
       not_4_out, not_5_out, not_6_out, not_7_out, not_8_out, not_9_out, not_10_out, not_11_out, not_12_out,
       not_13_out, not_14_out, not_15_out, not_16_out, not_17_out, not_18_out, not_19_out, not_20_out,
       not_21_out, not_22_out, not_23_out, not_24_out, not_25_out, not_26_out, not_27_out, not_28_out;

  DuoBinEnc duobinenc_1 (
    .D0(D0), .D1(D1), .D2(D2), .D3(D3), .D4(D4), .D5(D5), .D6(D6), .D7(D7), .D8(D8), .D9(D9), .DA(DA),
    .DB(DB), .B3(duobinenc_1_b3), .B2(duobinenc_1_b2), .B1(duobinenc_1_b1), .B0(duobinenc_1_b0));
  not not_1 (not_1_out, duobinenc_1_b3);
  not not_2 (not_2_out, duobinenc_1_b2);
  not not_3 (not_3_out, duobinenc_1_b1);
  not not_4 (not_4_out, duobinenc_1_b0);
  not not_5 (not_5_out, duobinenc_1_b3);
  not not_6 (not_6_out, duobinenc_1_b2);
  not not_7 (not_7_out, duobinenc_1_b1);
  not not_8 (not_8_out, duobinenc_1_b3);
  not not_9 (not_9_out, duobinenc_1_b2);
  not not_10 (not_10_out, duobinenc_1_b0);
  not not_11 (not_11_out, duobinenc_1_b3);
  not not_12 (not_12_out, duobinenc_1_b2);
  not not_13 (not_13_out, duobinenc_1_b3);
  not not_14 (not_14_out, duobinenc_1_b1);
  not not_15 (not_15_out, duobinenc_1_b0);
  not not_16 (not_16_out, duobinenc_1_b3);
  not not_17 (not_17_out, duobinenc_1_b1);
  not not_18 (not_18_out, duobinenc_1_b3);
  not not_19 (not_19_out, duobinenc_1_b0);
  not not_20 (not_20_out, duobinenc_1_b3);
  not not_21 (not_21_out, duobinenc_1_b2);
  not not_22 (not_22_out, duobinenc_1_b1);
  not not_23 (not_23_out, duobinenc_1_b0);
  not not_24 (not_24_out, duobinenc_1_b2);
  not not_25 (not_25_out, duobinenc_1_b1);
  not not_26 (not_26_out, duobinenc_1_b2);
  not not_27 (not_27_out, duobinenc_1_b0);
  not not_28 (not_28_out, duobinenc_1_b2);
  ANDGate andgate_1 (.A(not_1_out), .B(not_2_out), .C(not_3_out), .D(not_4_out), .O(oktal00));
  ANDGate andgate_2 (.A(not_5_out), .B(not_6_out), .C(not_7_out), .D(duobinenc_1_b0), .O(oktal01));
  ANDGate andgate_3 (.A(not_8_out), .B(not_9_out), .C(duobinenc_1_b1), .D(not_10_out), .O(oktal02));
  ANDGate andgate_4 (.A(not_11_out), .B(not_12_out), .C(duobinenc_1_b1), .D(duobinenc_1_b0), .O(oktal03));
  ANDGate andgate_5 (.A(not_13_out), .B(duobinenc_1_b2), .C(not_14_out), .D(not_15_out), .O(oktal04));
  ANDGate andgate_6 (.A(not_16_out), .B(duobinenc_1_b2), .C(not_17_out), .D(duobinenc_1_b0), .O(oktal05));
  ANDGate andgate_7 (.A(not_18_out), .B(duobinenc_1_b2), .C(duobinenc_1_b1), .D(not_19_out), .O(oktal06));
  ANDGate andgate_8 (.A(not_20_out), .B(duobinenc_1_b2), .C(duobinenc_1_b1), .D(duobinenc_1_b0), .O(oktal07));
  ANDGate andgate_9 (.A(duobinenc_1_b3), .B(not_21_out), .C(not_22_out), .D(not_23_out), .O(oktal10));
  ANDGate andgate_10 (.A(duobinenc_1_b3), .B(not_24_out), .C(not_25_out), .D(duobinenc_1_b0), .O(oktal11));
  ANDGate andgate_11 (.A(duobinenc_1_b3), .B(not_26_out), .C(duobinenc_1_b1), .D(not_27_out), .O(oktal12));
  ANDGate andgate_12 (.A(duobinenc_1_b3), .B(not_28_out), .C(duobinenc_1_b1), .D(duobinenc_1_b0), .O(oktal13));

  // Notes on the sheet:
  //   Misalkan DB = 1, maka oktal13 akan bernilai 1 
  //   Karena hasil konversi "B" dalam basis 12 ke Oktal akan bernilai "13"
endmodule
