// Logisim project LAB5_FEIN_2506599144_JovanFinesta.circ as structural Verilog: 2 circuits, main circuit Sequential
module Sequential (
  input  X,
  output O
);

  wire CLK_out, combinational_1_d0, combinational_1_d1, combinational_1_d2, D0_q, D1_q, D2_q;

  Clock CLK (.out(CLK_out));
  Combinational combinational_1 (
    .Y2(D2_q), .Y1(D1_q), .Y0(D0_q), .X(X), .D2(combinational_1_d2), .D1(combinational_1_d1),
    .D0(combinational_1_d0), .O(O));
  D_Flip_Flop D2 (.D(combinational_1_d2), .clk(CLK_out), .Q(D2_q));  // open: Qn, preset, reset
  D_Flip_Flop D1 (.D(combinational_1_d1), .clk(CLK_out), .Q(D1_q));  // open: Qn, preset, reset
  D_Flip_Flop D0 (.D(combinational_1_d0), .clk(CLK_out), .Q(D0_q));  // open: Qn, preset, reset
endmodule

module Combinational (
  input  Y2,
  input  Y1,
  input  Y0,
  input  X,
  output D2,
  output D1,
  output D0,
  output O
);

  wire and_2_out, and_3_out, and_4_out, and_5_out, and_6_out, not_1_out, not_2_out, not_3_out;

  not not_1 (not_1_out, Y1);
  not not_2 (not_2_out, Y0);
  not not_3 (not_3_out, X);
  and and_1 (D2, Y1, Y0, not_3_out);
  and and_2 (and_2_out, Y2, X);
  and and_3 (and_3_out, not_1_out, Y0, X);
  and and_4 (and_4_out, Y1, not_2_out, X);
  and and_5 (and_5_out, not_1_out, not_3_out);
  and and_6 (and_6_out, Y1, not_2_out);
  or or_1 (D1, and_2_out, and_3_out, and_4_out);
  or or_2 (D0, and_5_out, and_6_out);

  assign O = Y2;
endmodule
