// Logisim project TM3_Lampiran.circ as structural Verilog: 6 circuits, main circuit Original_1A
module Original_1A (
  input  A,
  input  B,
  input  C,
  input  D,
  output O_Original
);

  wire and_1_out, and_2_out, and_3_out, and_4_out, not_1_out, not_2_out, or_1_out, or_2_out;

  not not_1 (not_1_out, D);
  not not_2 (not_2_out, B);
  and and_1 (and_1_out, B, not_1_out);
  and and_2 (and_2_out, B, D);
  and and_3 (and_3_out, C, not_2_out);
  and and_4 (and_4_out, B, C);
  or or_1 (or_1_out, A, and_1_out, and_2_out);
  or or_2 (or_2_out, and_3_out, and_4_out);
  or or_3 (O_Original, or_1_out, or_2_out);
endmodule

module Simplified_1A (
  input  A,
  input  B,
  input  C,
  input  D,
  output O_Simplified
);

  or or_1 (O_Simplified, A, B, C);
endmodule

module Original_1B (
  input  A,
  input  B,
  input  C,
  input  D,
  output O_Original
);

  wire and_1_out, and_2_out, and_3_out, and_4_out, and_5_out, and_6_out, and_7_out, and_8_out, and_9_out,
       not_1_out, not_2_out, not_3_out, not_4_out, not_5_out, not_6_out, not_7_out, or_1_out;

  not not_1 (not_1_out, B);
  not not_2 (not_2_out, D);
  not not_3 (not_3_out, A);
  not not_4 (not_4_out, C);
  or or_1 (or_1_out, not_2_out, not_3_out);
  and and_1 (and_1_out, C, D);
  and and_2 (and_2_out, A, B);
  not not_5 (not_5_out, or_1_out);
  not not_6 (not_6_out, and_1_out);
  not not_7 (not_7_out, and_2_out);
  and and_3 (and_3_out, D, A, B);
  and and_4 (and_4_out, D, C, B);
  and and_5 (and_5_out, not_1_out, not_5_out, not_4_out);
  and and_6 (and_6_out, not_1_out, D, C, not_3_out);
  and and_7 (and_7_out, A, B, not_6_out);
  and and_8 (and_8_out, B, not_2_out, C);
  and and_9 (and_9_out, not_7_out, D, C);
  or or_2 (O_Original, B, and_3_out, and_4_out, and_5_out, and_6_out, and_7_out, and_8_out, and_9_out);
endmodule

module Simplified_1B (
  input  A,
  input  B,
  input  C,
  input  D,
  output O_Simplified
);

  wire and_1_out, or_1_out;

  or or_1 (or_1_out, A, C);
  and and_1 (and_1_out, D, or_1_out);
  or or_2 (O_Simplified, B, and_1_out);
endmodule

module TRUTHTest_3ab (
  input  A,
  input  B,
  input  C,
  input  D,
  output Oa,
  output Ob
);

  wire and_1_out, and_2_out, not_1_out, or_1_out;

  and and_1 (and_1_out, A, not_1_out);
  not not_1 (not_1_out, B);
  and and_2 (and_2_out, C, D);
  or or_1 (or_1_out, B, C);
  or or_2 (Oa, and_1_out, and_2_out);
  and and_3 (Ob, A, or_1_out);
endmodule

module Ori_NAND_4c (
  input  A,
  input  B,
  input  C,
  input  D,
  output O_original,
  output O_nand
);

  wire and_1_out, and_2_out, nand_1_out, nand_2_out, nand_3_out, nand_4_out, nand_5_out, nand_6_out,
       nand_7_out, or_1_out;

  or or_1 (or_1_out, A, C);
  nand nand_1 (nand_1_out, A, A);
  nand nand_2 (nand_2_out, C, C);
  nand nand_3 (nand_3_out, B, B);
  nand nand_4 (nand_4_out, D, D);
  and and_1 (and_1_out, D, or_1_out);
  and and_2 (and_2_out, ~B, ~D);  // AND_Gate
  nand nand_5 (nand_5_out, nand_1_out, nand_2_out);
  or or_2 (O_original, and_1_out, and_2_out);
  nand nand_6 (nand_6_out, D, nand_5_out);
  nand nand_7 (nand_7_out, nand_3_out, nand_4_out);
  nand nand_8 (O_nand, nand_6_out, nand_7_out);

  // Notes on the sheet:
  //   ORIGINAL
  //   ONLY NANDs
endmodule
