// Logisim project TM4_FEIN_2506599144_JovanFinesta.circ as structural Verilog: 8 circuits, main circuit Circ1A
module Circ1A_RancanganAwal (
  input  ENABLE,
  input  S2,
  input  S1,
  input  S0,
  output A0,
  output A1,
  output A2,
  output A3,
  output A4,
  output A5,
  output A6,
  output A7
);

  wire not_1_out, not_2_out, not_3_out, Q1_out, Q2_out, Q3_out, Q4_out, T1_out, T2_out;

  and T1 (T1_out, ENABLE, not_1_out);
  not not_1 (not_1_out, S2);
  and T2 (T2_out, ENABLE, S2);
  not not_2 (not_2_out, S1);
  not not_3 (not_3_out, S0);
  and Q1 (Q1_out, not_2_out, not_3_out);
  and Q2 (Q2_out, not_2_out, S0);
  and Q3 (Q3_out, S1, not_3_out);
  and Q4 (Q4_out, S1, S0);
  and and_1 (A0, T1_out, Q1_out);
  and and_2 (A1, T1_out, Q2_out);
  and and_3 (A2, T1_out, Q3_out);
  and and_4 (A3, T1_out, Q4_out);
  and and_5 (A4, T2_out, Q1_out);
  and and_6 (A5, T2_out, Q2_out);
  and and_7 (A6, T2_out, Q3_out);
  and and_8 (A7, T2_out, Q4_out);

  // Notes on the sheet:
  //   Circ1A, Sebelum Re-Mapping
endmodule

module Circ1A (
  input  ENABLE,
  input  S2,
  input  S1,
  input  S0,
  output A0,
  output A1,
  output A2,
  output A3,
  output A4,
  output A5,
  output A6,
  output A7
);

  wire nor_1_out, nor_2_out, nor_3_out, nor_4_out, nor_5_out, nor_6_out, nor_7_out, nor_8_out, nor_9_out,
       nor_10_out, nor_11_out, nor_12_out, nor_13_out, nor_14_out, nor_15_out, nor_16_out, nor_17_out;

  nor nor_1 (nor_1_out, ENABLE, ENABLE);
  nor nor_2 (nor_2_out, nor_1_out, nor_6_out);
  nor nor_3 (nor_3_out, nor_2_out, nor_2_out);
  nor nor_4 (nor_4_out, S2, S2);
  nor nor_5 (nor_5_out, S1, S1);
  nor nor_6 (nor_6_out, nor_4_out, nor_4_out);
  nor nor_7 (nor_7_out, nor_1_out, nor_4_out);
  nor nor_8 (nor_8_out, nor_7_out, nor_7_out);
  nor nor_9 (nor_9_out, S0, S0);
  nor nor_10 (nor_10_out, S1, S0);
  nor nor_11 (nor_11_out, nor_10_out, nor_10_out);
  nor nor_12 (nor_12_out, S1, nor_9_out);
  nor nor_13 (nor_13_out, nor_12_out, nor_12_out);
  nor nor_14 (nor_14_out, nor_5_out, S0);
  nor nor_15 (nor_15_out, nor_14_out, nor_14_out);
  nor nor_16 (nor_16_out, nor_5_out, nor_9_out);
  nor nor_17 (nor_17_out, nor_16_out, nor_16_out);
  nor nor_18 (A0, nor_3_out, nor_11_out);
  nor nor_19 (A1, nor_3_out, nor_13_out);
  nor nor_20 (A2, nor_3_out, nor_15_out);
  nor nor_21 (A3, nor_3_out, nor_17_out);
  nor nor_22 (A4, nor_8_out, nor_11_out);
  nor nor_23 (A5, nor_8_out, nor_13_out);
  nor nor_24 (A6, nor_8_out, nor_15_out);
  nor nor_25 (A7, nor_8_out, nor_17_out);

  // Notes on the sheet:
  //   Circ1A, setelah Re-Mapping ke NOR only
endmodule

module Circ1B_RancanganAwal (
  input  S2,
  input  S1,
  input  S0,
  input  A0,
  input  A1,
  input  A2,
  input  A3,
  input  A4,
  input  A5,
  input  A6,
  input  A7,
  output F
);

  wire and_1_out, and_2_out, and_3_out, and_4_out, and_5_out, and_6_out, and_7_out, and_8_out, not_1_out,
       not_2_out, not_3_out;

  not not_1 (not_1_out, S2);
  not not_2 (not_2_out, S1);
  not not_3 (not_3_out, S0);
  and and_1 (and_1_out, A0, not_1_out, not_2_out, not_3_out);
  and and_2 (and_2_out, A1, not_1_out, not_2_out, S0);
  and and_3 (and_3_out, A2, not_1_out, S1, not_3_out);
  and and_4 (and_4_out, A3, not_1_out, S1, S0);
  and and_5 (and_5_out, A4, S2, not_2_out, not_3_out);
  and and_6 (and_6_out, A5, S2, not_2_out, S0);
  and and_7 (and_7_out, A6, S2, S1, not_3_out);
  and and_8 (and_8_out, A7, S2, S1, S0);
  or or_1 (F, and_1_out, and_2_out, and_3_out, and_4_out, and_5_out, and_6_out, and_7_out, and_8_out);

  // Notes on the sheet:
  //   Circ1B, sebelum re-Mapping
endmodule

module Circ1B (
  input  S2,
  input  S1,
  input  S0,
  input  A0,
  input  A1,
  input  A2,
  input  A3,
  input  A4,
  input  A5,
  input  A6,
  input  A7,
  output F
);

  wire nor_1_out, nor_2_out, nor_3_out, nor_4_out, nor_5_out, nor_6_out, nor_7_out, nor_8_out, nor_9_out,
       nor_10_out, nor_11_out, nor_12_out, nor_13_out, nor_14_out, nor_15_out, nor_16_out, nor_17_out,
       nor_18_out, nor_19_out, nor_20_out;

  nor nor_1 (nor_1_out, S2, S2);
  nor nor_2 (nor_2_out, S1, S1);
  nor nor_3 (nor_3_out, S0, S0);
  nor nor_4 (nor_4_out, A0, A0);
  nor nor_5 (nor_5_out, A1, A1);
  nor nor_6 (nor_6_out, A2, A2);
  nor nor_7 (nor_7_out, A3, A3);
  nor nor_8 (nor_8_out, A4, A4);
  nor nor_9 (nor_9_out, A5, A5);
  nor nor_10 (nor_10_out, A6, A6);
  nor nor_11 (nor_11_out, A7, A7);
  nor nor_12 (nor_12_out, nor_4_out, S2, S1, S0);
  nor nor_13 (nor_13_out, nor_5_out, S2, S1, nor_3_out);
  nor nor_14 (nor_14_out, nor_6_out, S2, nor_2_out, S0);
  nor nor_15 (nor_15_out, nor_7_out, S2, nor_2_out, nor_3_out);
  nor nor_16 (nor_16_out, nor_8_out, nor_1_out, S1, S0);
  nor nor_17 (nor_17_out, nor_9_out, nor_1_out, S1, nor_3_out);
  nor nor_18 (nor_18_out, nor_10_out, nor_1_out, nor_2_out, S0);
  nor nor_19 (nor_19_out, nor_11_out, nor_1_out, nor_2_out, nor_3_out);
  nor nor_20 (nor_20_out, nor_12_out, nor_13_out, nor_14_out, nor_15_out, nor_16_out, nor_17_out, nor_18_out, nor_19_out);
  nor nor_21 (F, nor_20_out, nor_20_out);

  // Notes on the sheet:
  //   Circ1B, setelah re-mapping (NOR only)
endmodule

module Circ2 (
  input  W,
  input  X,
  input  Y,
  input  Z,
  output A,
  output B,
  output C,
  output D
);

  wire multiplexer_4_out, multiplexer_5_out, not_1_out;

  not not_1 (not_1_out, W);
  Multiplexer #(.select(2)) multiplexer_1 (.in0(1'b0), .in1(1'b0), .in2(1'b1), .in3(1'b1), .out(A), .sel({W, X}));
  Multiplexer #(.select(2)) multiplexer_2 (.in0(1'b0), .in1(1'b1), .in2(1'b1), .in3(1'b0), .out(B), .sel({W, X}));
  Multiplexer #(.select(2)) multiplexer_3 (.in0(W), .in1(not_1_out), .in2(not_1_out), .in3(W), .out(C), .sel({X, Y}));
  Multiplexer #(.select(2)) multiplexer_4 (
    .in0(1'b0), .in1(1'b1), .in2(1'b1), .in3(1'b0), .out(multiplexer_4_out), .sel({Y, Z}));
  Multiplexer #(.select(2)) multiplexer_5 (
    .in0(1'b1), .in1(1'b0), .in2(1'b0), .in3(1'b1), .out(multiplexer_5_out), .sel({Y, Z}));
  Multiplexer #(.select(2)) multiplexer_6 (
    .in0(multiplexer_4_out), .in1(multiplexer_5_out), .in2(multiplexer_5_out), .in3(multiplexer_4_out),
    .out(D), .sel({W, X}));

  // Notes on the sheet:
  //   Circ2
endmodule

module Circ3A (
  input  A,
  input  B,
  input  C,
  input  D,
  output F
);

  wire and_1_out, and_2_out, not_1_out, not_2_out, not_3_out;

  not not_1 (not_1_out, B);
  not not_2 (not_2_out, C);
  not not_3 (not_3_out, D);
  and and_1 (and_1_out, A, C);
  and and_2 (and_2_out, not_2_out, not_3_out);
  or or_1 (F, not_1_out, and_1_out, and_2_out);

  // Notes on the sheet:
  //   Circ 3A
endmodule

module Circ3B (
  input  A,
  input  B,
  input  C,
  input  D,
  output F
);

  wire and_1_out, and_2_out, and_3_out, not_1_out, not_2_out, not_3_out;

  not not_1 (not_1_out, A);
  not not_2 (not_2_out, B);
  not not_3 (not_3_out, C);
  and and_1 (and_1_out, not_1_out, not_2_out);
  and and_2 (and_2_out, B, C, D);
  and and_3 (and_3_out, A, not_3_out, D);
  or or_1 (F, and_1_out, and_2_out, and_3_out);

  // Notes on the sheet:
  //   Circ 3B
endmodule

module Circ4 (
  input  t0,
  input  t1,
  input  t2,
  input  t3,
  input  t4,
  input  t5,
  input  t6,
  output F2,
  output F1,
  output F0
);

  wire and_1_out, and_2_out, and_3_out, not_1_out, not_2_out, not_3_out, not_4_out, not_5_out, or_1_out,
       or_2_out;

  not not_1 (not_1_out, t4);
  not not_2 (not_2_out, t5);
  not not_3 (not_3_out, t6);
  not not_4 (not_4_out, t2);
  not not_5 (not_5_out, t4);
  or or_1 (or_1_out, t2, t3);
  and and_1 (and_1_out, t1, not_4_out, not_5_out);
  and and_2 (and_2_out, t3, not_5_out);
  and and_3 (and_3_out, not_1_out, not_2_out, or_1_out);
  or or_2 (or_2_out, and_1_out, and_2_out, t5);
  or or_3 (F2, t4, t5, t6);
  or or_4 (F1, and_3_out, t6);
  and and_4 (F0, not_3_out, or_2_out);

  // Notes on the sheet:
  //   Circ4
endmodule
