// Logisim project TM5_FEIN_2506599144_JovanFinesta.circ as structural Verilog: 2 circuits, main circuit Pitstop_BCD
module Pitstop_BCD (
  input  [3:0] A,
  input  [3:0] B,
  input  Cin,
  output [3:0] Sum,
  output Cout
);

  wire adder_1_cout, adder_1_out, adder_2_cout, adder_2_out, adder_3_cout, adder_3_out, adder_4_cout,
       adder_4_out, adder_5_cout, adder_6_cout, adder_7_cout, adder_8_cout, and_1_out, or_1_out, or_2_out;

  Adder #(.width(1)) adder_1 (.a(A[0]), .b(B[0]), .out(adder_1_out), .cin(Cin), .cout(adder_1_cout));
  Adder #(.width(1)) adder_2 (.a(A[1]), .b(B[1]), .out(adder_2_out), .cin(adder_1_cout), .cout(adder_2_cout));
  Adder #(.width(1)) adder_3 (.a(A[2]), .b(B[2]), .out(adder_3_out), .cin(adder_2_cout), .cout(adder_3_cout));
  Adder #(.width(1)) adder_4 (.a(A[3]), .b(B[3]), .out(adder_4_out), .cin(adder_3_cout), .cout(adder_4_cout));
  and and_1 (and_1_out, adder_4_out, or_2_out);
  or or_1 (or_1_out, adder_4_cout, and_1_out);
  or or_2 (or_2_out, adder_3_out, adder_2_out);
  Adder #(.width(1)) adder_5 (.a(adder_1_out), .b(1'b0), .out(Sum[0]), .cin(1'b0), .cout(adder_5_cout));
  Adder #(.width(1)) adder_6 (.a(adder_2_out), .b(or_1_out), .out(Sum[1]), .cin(adder_5_cout), .cout(adder_6_cout));
  Adder #(.width(1)) adder_7 (.a(adder_3_out), .b(or_1_out), .out(Sum[2]), .cin(adder_6_cout), .cout(adder_7_cout));
  Adder #(.width(1)) adder_8 (.a(adder_4_out), .b(1'b0), .out(Sum[3]), .cin(adder_7_cout), .cout(adder_8_cout));
  or or_3 (Cout, adder_8_cout, or_1_out);
endmodule

module Pitstop_BCD_with_Signal (
  input  [3:0] A,
  input  [3:0] B,
  input  Cin,
  output [3:0] Sum,
  output Cout,
  output K
);

  wire adder_1_cout, adder_1_out, adder_2_cout, adder_2_out, adder_3_cout, adder_3_out, adder_4_cout,
       adder_4_out, adder_5_cout, adder_6_cout, adder_7_cout, adder_8_cout, and_1_out, or_2_out;

  Adder #(.width(1)) adder_1 (.a(A[0]), .b(B[0]), .out(adder_1_out), .cin(Cin), .cout(adder_1_cout));
  Adder #(.width(1)) adder_2 (.a(A[1]), .b(B[1]), .out(adder_2_out), .cin(adder_1_cout), .cout(adder_2_cout));
  Adder #(.width(1)) adder_3 (.a(A[2]), .b(B[2]), .out(adder_3_out), .cin(adder_2_cout), .cout(adder_3_cout));
  Adder #(.width(1)) adder_4 (.a(A[3]), .b(B[3]), .out(adder_4_out), .cin(adder_3_cout), .cout(adder_4_cout));
  and and_1 (and_1_out, adder_4_out, or_2_out);
  or or_1 (K, adder_4_cout, and_1_out);
  or or_2 (or_2_out, adder_3_out, adder_2_out);
  Adder #(.width(1)) adder_5 (.a(adder_1_out), .b(1'b0), .out(Sum[0]), .cin(1'b0), .cout(adder_5_cout));
  Adder #(.width(1)) adder_6 (.a(adder_2_out), .b(K), .out(Sum[1]), .cin(adder_5_cout), .cout(adder_6_cout));
  Adder #(.width(1)) adder_7 (.a(adder_3_out), .b(K), .out(Sum[2]), .cin(adder_6_cout), .cout(adder_7_cout));
  Adder #(.width(1)) adder_8 (.a(adder_4_out), .b(1'b0), .out(Sum[3]), .cin(adder_7_cout), .cout(adder_8_cout));
  or or_3 (Cout, adder_8_cout, K);
endmodule
