// Logisim project TM6_FEIN_2506599144_JovanFinesta.circ as structural Verilog: 3 circuits, main circuit Combinational2F
module Combinational2F (
  input  Y2,
  input  Y1,
  input  Y0,
  input  X,
  output D2,
  output D1,
  output D0,
  output Z
);

  wire and_1_out, and_2_out, and_3_out, and_4_out, and_5_out, and_6_out, and_7_out, and_8_out, and_9_out,
       and_10_out, and_11_out, not_1_out, not_2_out, not_3_out, not_4_out, xor_1_out;

  not not_1 (not_1_out, Y2);
  not not_2 (not_2_out, Y1);
  not not_3 (not_3_out, Y0);
  not not_4 (not_4_out, X);
  and and_1 (and_1_out, Y2, not_3_out);
  and and_2 (and_2_out, not_2_out, Y0, X);
  and and_3 (and_3_out, not_1_out, Y1, Y0);
  and and_4 (and_4_out, Y2, Y0, X);
  and and_5 (and_5_out, not_1_out, Y0, not_4_out);
  and and_6 (and_6_out, Y2, Y1, not_3_out, not_4_out);
  and and_7 (and_7_out, not_1_out, Y1, not_3_out, X);
  and and_8 (and_8_out, Y2, not_3_out, not_4_out);
  and and_9 (and_9_out, not_1_out, not_3_out, X);
  and and_10 (and_10_out, Y2, Y1, Y0, X);
  and and_11 (and_11_out, not_1_out, Y1, Y0, not_4_out);
  xor xor_1 (xor_1_out, Y2, Y0, X);
  or or_1 (D2, and_1_out, and_2_out, and_3_out);
  or or_2 (D1, and_4_out, and_5_out, and_6_out, and_7_out);
  or or_3 (D0, and_8_out, and_9_out, and_10_out, and_11_out);
  and and_12 (Z, Y1, xor_1_out);
endmodule

module Sequential2F (
  input  X,
  output Z
);

  wire CLK_out, combinational2f_1_d0, combinational2f_1_d1, combinational2f_1_d2, D0_q, D1_q, D2_q;

  Combinational2F combinational2f_1 (
    .Y2(D2_q), .Y1(D1_q), .Y0(D0_q), .X(X), .D2(combinational2f_1_d2), .D1(combinational2f_1_d1),
    .D0(combinational2f_1_d0), .Z(Z));
  Clock CLK (.out(CLK_out));
  D_Flip_Flop D2 (.D(combinational2f_1_d2), .clk(CLK_out), .Q(D2_q));  // open: Qn, preset, reset
  D_Flip_Flop D1 (.D(combinational2f_1_d1), .clk(CLK_out), .Q(D1_q));  // open: Qn, preset, reset
  D_Flip_Flop D0 (.D(combinational2f_1_d0), .clk(CLK_out), .Q(D0_q));  // open: Qn, preset, reset
endmodule

module Circuit3 (
  input  X,
  output Z
);

  wire and_1_out, and_2_out, and_3_out, and_4_out, CLK_out, not_1_out, or_1_out, Y0_q, Y1_q, Y1_qn;

  not not_1 (not_1_out, X);
  and and_1 (and_1_out, Y1_q, Y0_q, not_1_out);
  and and_2 (and_2_out, Y0_q, not_1_out);
  and and_3 (and_3_out, Y1_q, X);
  and and_4 (and_4_out, Y1_qn, not_1_out);
  or or_1 (or_1_out, and_3_out, and_4_out);
  Clock CLK (.out(CLK_out));
  J_K_Flip_Flop Y2 (.J(and_1_out), .K(and_1_out), .clk(CLK_out), .Q(Z));  // open: Qn, preset, reset
  J_K_Flip_Flop Y1 (.J(and_2_out), .K(Y0_q), .clk(CLK_out), .Q(Y1_q), .Qn(Y1_qn));  // open: preset, reset
  J_K_Flip_Flop Y0 (.J(or_1_out), .K(1'b1), .clk(CLK_out), .Q(Y0_q));  // open: Qn, preset, reset
endmodule
