// Logisim project TM8_FEIN_2506599144_JovanFinesta.circ as structural Verilog: 2 circuits, main circuit CombinationalCirc4
module CombinationalCirc4 (
  input  A,
  input  B,
  input  S,
  output DA,
  output DB
);

  wire and_1_out, and_2_out, and_3_out, not_1_out, not_2_out, not_3_out;

  not not_1 (not_1_out, B);
  not not_2 (not_2_out, A);
  not not_3 (not_3_out, S);
  and and_1 (and_1_out, not_2_out, not_3_out);
  and and_2 (and_2_out, not_2_out, not_1_out);
  and and_3 (and_3_out, A, B, S);
  or or_1 (DA, and_1_out, and_2_out, and_3_out);
  xor xor_1 (DB, B, S);
endmodule

module SequentialCirc4 (
  input  S,
  input  R,
  output A,
  output B
);

  wire CLK_out, combinationalcirc4_1_da, combinationalcirc4_1_db;

  Clock CLK (.out(CLK_out));
  CombinationalCirc4 combinationalcirc4_1 (
    .A(A), .B(B), .S(S), .DA(combinationalcirc4_1_da), .DB(combinationalcirc4_1_db));
  D_Flip_Flop d_ff_1 (.D(combinationalcirc4_1_da), .clk(CLK_out), .Q(A), .reset(R));  // open: Qn, preset
  D_Flip_Flop d_ff_2 (.D(combinationalcirc4_1_db), .clk(CLK_out), .Q(B), .reset(R));  // open: Qn, preset
endmodule
