// Logisim project contohlab5.circ as structural Verilog: 2 circuits, main circuit Combinational
module Combinational (
  input  Y1,
  input  Y0,
  input  X,
  output D1,
  output D0,
  output Y
);

  wire and_1_out, and_2_out, not_1_out, not_2_out, not_3_out;

  not not_1 (not_1_out, Y1);
  not not_2 (not_2_out, Y0);
  not not_3 (not_3_out, X);
  and and_1 (and_1_out, Y0, X);
  and and_2 (and_2_out, Y1, X);
  and and_3 (D0, not_1_out, not_2_out, X);
  and and_4 (Y, Y1, not_3_out);
  or or_1 (D1, and_1_out, and_2_out);
endmodule

module Sequential (
  input  in_1,
  output out_2
);

  wire clock_1_out, combinational_1_d0, combinational_1_d1, d_ff_1_q, d_ff_2_q;

  Clock clock_1 (.out(clock_1_out));
  Combinational combinational_1 (
    .Y1(d_ff_1_q), .Y0(d_ff_2_q), .X(in_1), .D1(combinational_1_d1), .D0(combinational_1_d0), .Y(out_2));
  D_Flip_Flop d_ff_1 (.D(combinational_1_d1), .clk(clock_1_out), .Q(d_ff_1_q));  // open: Qn, preset, reset
  D_Flip_Flop d_ff_2 (.D(combinational_1_d0), .clk(clock_1_out), .Q(d_ff_2_q));  // open: Qn, preset, reset
endmodule
